// Logisim project NC16.circ as structural Verilog: 5 circuits, main circuit main
module main (
  input  in_1
);

  wire adder_2_cout, and_1_out, and_2_out, and_3_out, and_4_out, and_5_out, button_1_out, clock_1_out,
       clock_2_out, d_ff_1_q, d_ff_2_q, d_ff_3_q, decoder_1_out0, decoder_1_out1, decoder_1_out2,
       decoder_1_out3, decoder_1_out4, decoder_1_out5, decoder_1_out6, decoder_1_out7, decoder_1_out8,
       decoder_1_out9, decoder_1_out10, instruction_control_1_ie, multiplexer_11_out, not_1_out, not_2_out,
       not_3_out, not_4_out, not_5_out, not_7_out, not_8_out, not_9_out, not_11_out, not_12_out, not_13_out,
       not_14_out, not_15_out, not_16_out, not_17_out, not_18_out, not_19_out, not_20_out, not_21_out,
       not_22_out, not_23_out, not_24_out, not_25_out, not_26_out, RESET_out, right_shifter_1_carry_out;
  wire [0:0] not_6_out;
  wire [1:0] counter_1_q;
  wire [2:0] alu_1_carry_flag, Instruction_Register_p6, subtractor_1_bout;
  wire [3:0] Instruction_Decoder_out_2;
  wire [4:0] instruction_control_1_cpu_control_bus;
  wire [15:0] A_q, adder_1_out, adder_2_out, alu_1_alu_out, and_7_out, B_q, BP_q, C_q, D_q, decoder_2_out0,
       demultiplexer_1_out0, demultiplexer_1_out1, demultiplexer_2_out0, demultiplexer_2_out1,
       demultiplexer_3_out0, demultiplexer_3_out1, demultiplexer_3_out2, demultiplexer_3_out3,
       demultiplexer_3_out4, demultiplexer_3_out5, demultiplexer_3_out6, demultiplexer_3_out7,
       demultiplexer_4_out0, demultiplexer_4_out1, demultiplexer_4_out2, demultiplexer_4_out3,
       demultiplexer_4_out4, demultiplexer_4_out6, demultiplexer_4_out7, dipswitch_1_sw16, E_q,
       Input_port_sw16, instruction_control_1_mem_data_out, instruction_control_1_operand,
       instruction_control_1_pc_data_out, Instruction_Register_p3, Instruction_Register_p4,
       Instruction_Register_p5, MEMADDR_q, MEMVAL_q, multiplexer_1_out, multiplexer_2_out, multiplexer_3_out,
       multiplexer_4_out, multiplexer_5_out, multiplexer_6_out, multiplexer_7_out, multiplexer_8_out,
       multiplexer_9_out, multiplexer_10_out, multiplexer_12_out, multiplexer_13_out, multiplexer_14_out,
       multiplexer_15_out, multiplexer_16_out, multiplexer_17_out, multiplexer_18_out, multiplexer_20_out,
       multiplexer_21_out, multiplexer_22_out, multiplier_1_cout, multiplier_1_out, not_10_out, or_1_out,
       Output_port_q, PC_q, RAM_1_dout, register_1_q, register_2_q, registers_1_a_out, registers_1_b_out,
       registers_1_bp_out, registers_1_c_out, registers_1_d_out, registers_1_e_out, registers_1_memaddr_out,
       registers_1_memval_out, registers_1_output_out, registers_1_sp_out, right_shifter_1_output_bus_1,
       SP_q, subtractor_1_out, xor_1_out;
  wire [15:3] FLAGS_q;
  wire [17:0] instruction_control_1_cpu_control_bus_2;
  wire [18:0] Instruction_Decoder_out;
  wire [19:16] and_6_out;

  TTY #(.cols(64), .rows(16)) tty_1 (.data(Output_port_q[6:0]), .clk(clock_1_out), .we(decoder_1_out8), .clr(in_1));
  DipSwitch #(.number(16)) Input_port (
    .sw1(Input_port_sw16[15]), .sw2(Input_port_sw16[14]), .sw3(Input_port_sw16[13]),
    .sw4(Input_port_sw16[12]), .sw5(Input_port_sw16[11]), .sw6(Input_port_sw16[10]),
    .sw7(Input_port_sw16[9]), .sw8(Input_port_sw16[8]), .sw9(Input_port_sw16[7]), .sw10(Input_port_sw16[6]),
    .sw11(Input_port_sw16[5]), .sw12(Input_port_sw16[4]), .sw13(Input_port_sw16[3]),
    .sw14(Input_port_sw16[2]), .sw15(Input_port_sw16[1]), .sw16(Input_port_sw16[0]));
  Clock clock_1 (.out(clock_1_out));
  Button RESET (.out(RESET_out));
  and and_1 (and_1_out, clock_1_out, not_9_out);
  Decoder #(.select(4)) decoder_1 (
    .out0(decoder_1_out0), .out1(decoder_1_out1), .out2(decoder_1_out2), .out3(decoder_1_out3),
    .out4(decoder_1_out4), .out5(decoder_1_out5), .out6(decoder_1_out6), .out7(decoder_1_out7),
    .out8(decoder_1_out8), .out9(decoder_1_out9), .out10(decoder_1_out10), .sel(Instruction_Decoder_out[6:3]));  // open: out11, out12, out13, out14, out15, en
  DipSwitch #(.number(16)) dipswitch_1 (
    .sw1(dipswitch_1_sw16[15]), .sw2(dipswitch_1_sw16[14]), .sw3(dipswitch_1_sw16[13]),
    .sw4(dipswitch_1_sw16[12]), .sw5(dipswitch_1_sw16[11]), .sw6(dipswitch_1_sw16[10]),
    .sw7(dipswitch_1_sw16[9]), .sw8(dipswitch_1_sw16[8]), .sw9(dipswitch_1_sw16[7]),
    .sw10(dipswitch_1_sw16[6]), .sw11(dipswitch_1_sw16[5]), .sw12(dipswitch_1_sw16[4]),
    .sw13(dipswitch_1_sw16[3]), .sw14(dipswitch_1_sw16[2]), .sw15(dipswitch_1_sw16[1]),
    .sw16(dipswitch_1_sw16[0]));
  Button button_1 (.out(button_1_out));
  LedBar #(.matrixcols(16)) Output_port_LED (
    .led0(registers_1_output_out[15]), .led1(registers_1_output_out[14]), .led2(registers_1_output_out[13]),
    .led3(registers_1_output_out[12]), .led4(registers_1_output_out[11]), .led5(registers_1_output_out[10]),
    .led6(registers_1_output_out[9]), .led7(registers_1_output_out[8]), .led8(registers_1_output_out[7]),
    .led9(registers_1_output_out[6]), .led10(registers_1_output_out[5]), .led11(registers_1_output_out[4]),
    .led12(registers_1_output_out[3]), .led13(registers_1_output_out[2]), .led14(registers_1_output_out[1]),
    .led15(registers_1_output_out[0]));
  Clock clock_2 (.out(clock_2_out));
  and and_2 (and_2_out, clock_2_out, not_5_out);
  LedBar #(.matrixcols(16)) LedBar_1 (
    .led0(multiplexer_20_out[15]), .led1(multiplexer_20_out[14]), .led2(multiplexer_20_out[13]),
    .led3(multiplexer_20_out[12]), .led4(multiplexer_20_out[11]), .led5(multiplexer_20_out[10]),
    .led6(multiplexer_20_out[9]), .led7(multiplexer_20_out[8]), .led8(multiplexer_20_out[7]),
    .led9(multiplexer_20_out[6]), .led10(multiplexer_20_out[5]), .led11(multiplexer_20_out[4]),
    .led12(multiplexer_20_out[3]), .led13(multiplexer_20_out[2]), .led14(multiplexer_20_out[1]),
    .led15(multiplexer_20_out[0]));
  Register #(.width(16)) MEMVAL (
    .D(multiplexer_1_out), .en(decoder_1_out10), .clk(and_1_out), .Q(MEMVAL_q), .clr(RESET_out));
  Multiplexer #(.width(16)) multiplexer_1 (
    .in0(MEMVAL_q), .in1(multiplexer_20_out), .out(multiplexer_1_out), .sel(decoder_1_out10));
  Register #(.width(16)) MEMADDR (
    .D(multiplexer_2_out), .en(decoder_1_out9), .clk(and_1_out), .Q(MEMADDR_q), .clr(RESET_out));
  Multiplexer #(.width(16)) multiplexer_2 (
    .in0(MEMADDR_q), .in1(multiplexer_20_out), .out(multiplexer_2_out), .sel(decoder_1_out9));
  Register #(.width(16)) A (.D(multiplexer_3_out), .en(decoder_1_out0), .clk(and_1_out), .Q(A_q), .clr(RESET_out));
  Multiplexer #(.width(16)) multiplexer_3 (
    .in0(A_q), .in1(multiplexer_20_out), .out(multiplexer_3_out), .sel(decoder_1_out0));
  Register #(.width(16)) B (.D(multiplexer_4_out), .en(decoder_1_out1), .clk(and_1_out), .Q(B_q), .clr(RESET_out));
  Multiplexer #(.width(16)) multiplexer_4 (
    .in0(B_q), .in1(multiplexer_20_out), .out(multiplexer_4_out), .sel(decoder_1_out1));
  Register #(.width(16)) C (.D(multiplexer_5_out), .en(decoder_1_out2), .clk(and_1_out), .Q(C_q), .clr(RESET_out));
  Multiplexer #(.width(16)) multiplexer_5 (
    .in0(C_q), .in1(multiplexer_20_out), .out(multiplexer_5_out), .sel(decoder_1_out2));
  Register #(.width(16)) D (.D(multiplexer_6_out), .en(decoder_1_out3), .clk(and_1_out), .Q(D_q), .clr(RESET_out));
  Multiplexer #(.width(16)) multiplexer_6 (
    .in0(D_q), .in1(multiplexer_20_out), .out(multiplexer_6_out), .sel(decoder_1_out3));
  Register #(.width(16)) E (.D(multiplexer_7_out), .en(decoder_1_out4), .clk(and_1_out), .Q(E_q), .clr(RESET_out));
  Multiplexer #(.width(16)) multiplexer_7 (
    .in0(E_q), .in1(multiplexer_20_out), .out(multiplexer_7_out), .sel(decoder_1_out4));
  Register #(.width(16)) BP (.D(multiplexer_8_out), .en(decoder_1_out5), .clk(and_1_out), .Q(BP_q), .clr(RESET_out));
  Multiplexer #(.width(16)) multiplexer_8 (
    .in0(BP_q), .in1(multiplexer_20_out), .out(multiplexer_8_out), .sel(decoder_1_out5));
  Register #(.width(16)) SP (.D(multiplexer_9_out), .en(decoder_1_out6), .clk(and_1_out), .Q(SP_q), .clr(RESET_out));
  Multiplexer #(.width(16)) multiplexer_9 (
    .in0(SP_q), .in1(multiplexer_20_out), .out(multiplexer_9_out), .sel(decoder_1_out6));
  Multiplexer #(.width(16)) multiplexer_10 (
    .in0(PC_q), .in1(multiplexer_20_out), .out(multiplexer_10_out), .sel(multiplexer_11_out));
  Multiplexer multiplexer_11 (.in0(decoder_1_out7), .in1(1'b1), .out(multiplexer_11_out), .sel(and_3_out));
  and and_3 (and_3_out, d_ff_1_q, not_1_out);
  not not_1 (not_1_out, not_2_out);
  Register #(.width(16)) Output_port (
    .D(multiplexer_12_out), .en(decoder_1_out8), .clk(and_1_out), .Q(Output_port_q), .clr(RESET_out));
  Multiplexer #(.width(16)) multiplexer_12 (
    .in0(Output_port_q), .in1(multiplexer_20_out), .out(multiplexer_12_out), .sel(decoder_1_out8));
  Counter #(.max('hffff), .width(16)) PC (
    .clr(RESET_out), .load(multiplexer_11_out), .clk(and_1_out), .D(multiplexer_13_out), .Q(PC_q));  // open: up, count, carry
  Multiplexer #(.width(16)) multiplexer_13 (
    .in0(multiplexer_10_out), .in1(register_1_q), .out(multiplexer_13_out), .sel(and_3_out));
  LedBar #(.matrixcols(16)) LedBar_5 (
    .led0(Output_port_q[15]), .led1(Output_port_q[14]), .led2(Output_port_q[13]), .led3(Output_port_q[12]),
    .led4(Output_port_q[11]), .led5(Output_port_q[10]), .led6(Output_port_q[9]), .led7(Output_port_q[8]),
    .led8(Output_port_q[7]), .led9(Output_port_q[6]), .led10(Output_port_q[5]), .led11(Output_port_q[4]),
    .led12(Output_port_q[3]), .led13(Output_port_q[2]), .led14(Output_port_q[1]), .led15(Output_port_q[0]));
  Decoder #(.select(4)) decoder_2 (
    .out0(decoder_2_out0[0]), .out1(decoder_2_out0[1]), .out2(decoder_2_out0[2]), .out3(decoder_2_out0[3]),
    .out4(decoder_2_out0[4]), .out5(decoder_2_out0[5]), .out6(decoder_2_out0[6]), .out7(decoder_2_out0[7]),
    .out8(decoder_2_out0[8]), .out9(decoder_2_out0[9]), .out10(decoder_2_out0[10]),
    .out11(decoder_2_out0[11]), .out12(decoder_2_out0[12]), .out13(decoder_2_out0[13]),
    .out14(decoder_2_out0[14]), .out15(decoder_2_out0[15]), .sel(instruction_control_1_cpu_control_bus_2[5:2]));  // open: en
  LedBar #(.matrixcols(16)) LedBar_4 (
    .led0(PC_q[15]), .led1(PC_q[14]), .led2(PC_q[13]), .led3(PC_q[12]), .led4(PC_q[11]), .led5(PC_q[10]),
    .led6(PC_q[9]), .led7(PC_q[8]), .led8(PC_q[7]), .led9(PC_q[6]), .led10(PC_q[5]), .led11(PC_q[4]),
    .led12(PC_q[3]), .led13(PC_q[2]), .led14(PC_q[1]), .led15(PC_q[0]));
  Register #(.width(16)) register_1 (.D(PC_q), .en(1'b1), .clk(and_1_out), .Q(register_1_q), .clr(RESET_out));
  not not_2 (not_2_out, and_4_out);
  not not_3 (not_3_out, Instruction_Decoder_out[1]);
  and and_4 (and_4_out, not_3_out, not_4_out);
  not not_4 (not_4_out, Instruction_Decoder_out[2]);
  D_Flip_Flop d_ff_1 (.D(not_2_out), .clk(and_1_out), .Q(d_ff_1_q), .reset(RESET_out));  // open: Qn, preset
  Adder #(.width(16)) adder_1 (
    .a(MEMADDR_q), .b(Instruction_Register_p4), .out(adder_1_out), .cin(1'b0));  // open: cout
  registers registers_1 (
    .reg_data_in(multiplexer_16_out), .CLK(and_2_out), .RESET(button_1_out),
    .write_reg_select(decoder_2_out0), .memval_out(registers_1_memval_out),
    .memaddr_out(registers_1_memaddr_out), .a_out(registers_1_a_out), .b_out(registers_1_b_out),
    .c_out(registers_1_c_out), .d_out(registers_1_d_out), .e_out(registers_1_e_out),
    .bp_out(registers_1_bp_out), .sp_out(registers_1_sp_out), .output_out(registers_1_output_out));
  Instruction_Control instruction_control_1 (
    .mem_data_in(registers_1_memval_out), .mem_addr_in(registers_1_memaddr_out), .CLK(and_2_out),
    .pc_data_in(multiplexer_16_out), .pc_write_enable(decoder_2_out0[7]), .carry_flag(register_2_q[0]),
    .zero_flag(register_2_q[1]), .sign_flag(register_2_q[2]), .RESET(button_1_out),
    .mem_data_out(instruction_control_1_mem_data_out), .operand(instruction_control_1_operand),
    .pc_data_out(instruction_control_1_pc_data_out),
    .CPU_Control_BUS({instruction_control_1_cpu_control_bus_2[17], instruction_control_1_cpu_control_bus, instruction_control_1_cpu_control_bus_2[11:0]}),
    .IE(instruction_control_1_ie));
  Multiplexer #(.select(2), .width(16)) multiplexer_14 (
    .in0(PC_q), .in1(adder_1_out), .in2(Instruction_Register_p4), .out(multiplexer_14_out),
    .sel(Instruction_Decoder_out[2:1]));  // open: in3
  RAM #(.addrWidth(16), .dataWidth(16), .enables("line")) RAM_1 (
    .addr(multiplexer_14_out), .we(Instruction_Decoder_out[0]), .clk(and_1_out), .din(MEMVAL_q),
    .dout(RAM_1_dout));
  Multiplexer #(.select(4), .width(16)) multiplexer_15 (
    .in0(registers_1_a_out), .in1(registers_1_b_out), .in2(registers_1_c_out), .in3(registers_1_d_out),
    .in4(registers_1_e_out), .in5(registers_1_bp_out), .in6(registers_1_sp_out),
    .in7(instruction_control_1_operand), .in8(dipswitch_1_sw16), .in9(instruction_control_1_mem_data_out),
    .in10(instruction_control_1_pc_data_out), .in11(registers_1_memval_out), .out(multiplexer_15_out),
    .sel(instruction_control_1_cpu_control_bus[4:1]));  // open: in12, in13, in14, in15
  not not_5 (not_5_out, instruction_control_1_cpu_control_bus_2[17]);
  Multiplexer #(.width(16)) multiplexer_16 (
    .in0(demultiplexer_1_out0), .in1(alu_1_alu_out), .out(multiplexer_16_out),
    .sel(instruction_control_1_cpu_control_bus[0]));
  Demultiplexer #(.width(16)) demultiplexer_1 (
    .out0(demultiplexer_1_out0), .out1(demultiplexer_1_out1), .in(multiplexer_15_out),
    .sel(instruction_control_1_cpu_control_bus[0]));
  Multiplexer #(.select(3), .width(16)) multiplexer_17 (
    .in0(registers_1_a_out), .in1(registers_1_b_out), .in2(registers_1_c_out), .in3(registers_1_d_out),
    .in4(registers_1_e_out), .in5(registers_1_bp_out), .in6(registers_1_sp_out),
    .in7(instruction_control_1_operand), .out(multiplexer_17_out),
    .sel(instruction_control_1_cpu_control_bus_2[11:9]));
  LedBar #(.matrixcols(16)) LedBar_3 (
    .led0(demultiplexer_2_out0[15]), .led1(demultiplexer_2_out0[14]), .led2(demultiplexer_2_out0[13]),
    .led3(demultiplexer_2_out0[12]), .led4(demultiplexer_2_out0[11]), .led5(demultiplexer_2_out0[10]),
    .led6(demultiplexer_2_out0[9]), .led7(demultiplexer_2_out0[8]), .led8(demultiplexer_2_out0[7]),
    .led9(demultiplexer_2_out0[6]), .led10(demultiplexer_2_out0[5]), .led11(demultiplexer_2_out0[4]),
    .led12(demultiplexer_2_out0[3]), .led13(demultiplexer_2_out0[2]), .led14(demultiplexer_2_out0[1]),
    .led15(demultiplexer_2_out0[0]));
  Counter #(.max('h3), .width(2)) counter_1 (
    .clr(RESET_out), .load(and_6_out[16]), .clk(and_1_out), .D({1'b0, not_6_out[0]}), .Q(counter_1_q));  // open: up, count, carry
  Demultiplexer #(.width(16)) demultiplexer_2 (
    .out0(demultiplexer_2_out0), .out1(demultiplexer_2_out1), .in(multiplexer_18_out),
    .sel(Instruction_Decoder_out[13]));
  Multiplexer #(.select(4), .width(16)) multiplexer_18 (
    .in0(A_q), .in1(B_q), .in2(C_q), .in3(D_q), .in4(E_q), .in5(BP_q), .in6(SP_q),
    .in7(Instruction_Register_p4), .in8(Input_port_sw16), .in9(RAM_1_dout), .in10(PC_q), .in11(MEMVAL_q),
    .out(multiplexer_18_out), .sel(Instruction_Decoder_out_2));  // open: in12, in13, in14, in15
  // Shift_Register #(.length(2), .width(16)) Instruction_Register: pin names not known; wires that end beside it: RESET_out, and_1_out, Instruction_Register_p3, Instruction_Register_p4, Instruction_Register_p5, Instruction_Register_p6, Instruction_Register_p6
  Multiplexer #(.width(16)) multiplexer_19 (
    .in0(RAM_1_dout), .in1({16{1'b1}}), .out(Instruction_Register_p3), .sel(not_2_out));
  not not_6 (not_6_out[0], and_5_out);
  Multiplexer #(.width(16)) multiplexer_20 (
    .in0(demultiplexer_2_out0), .in1(multiplexer_22_out), .out(multiplexer_20_out),
    .sel(Instruction_Decoder_out[13]));
  Demultiplexer #(.select(3), .width(16)) demultiplexer_3 (
    .out0(demultiplexer_3_out0), .out1(demultiplexer_3_out1), .out2(demultiplexer_3_out2),
    .out3(demultiplexer_3_out3), .out4(demultiplexer_3_out4), .out5(demultiplexer_3_out5),
    .out6(demultiplexer_3_out6), .out7(demultiplexer_3_out7), .in(demultiplexer_2_out1),
    .sel(Instruction_Decoder_out[9:7]));
  and and_5 (and_5_out, Instruction_Decoder_out[3], Instruction_Decoder_out[4], Instruction_Decoder_out[5], not_7_out);
  Multiplexer #(.select(3), .width(16)) multiplexer_21 (
    .in0(A_q), .in1(B_q), .in2(C_q), .in3(D_q), .in4(E_q), .in5(BP_q), .in6(SP_q),
    .in7(Instruction_Register_p4), .out(multiplexer_21_out), .sel(Instruction_Register_p6));
  not not_7 (not_7_out, Instruction_Decoder_out[6]);
  Demultiplexer #(.select(3), .width(16)) demultiplexer_4 (
    .out0(demultiplexer_4_out0), .out1(demultiplexer_4_out1), .out2(demultiplexer_4_out2),
    .out3(demultiplexer_4_out3), .out4(demultiplexer_4_out4), .out6(demultiplexer_4_out6),
    .out7(demultiplexer_4_out7), .in(multiplexer_21_out), .sel(Instruction_Decoder_out[9:7]));  // open: out5
  not not_8 (not_8_out, counter_1_q[0]);
  and and_6 (and_6_out[16], not_8_out, counter_1_q[1]);
  ALU alu_1 (
    .in1_data_in(demultiplexer_1_out1), .in2_data_in(multiplexer_17_out),
    .ALU_function_select(instruction_control_1_cpu_control_bus_2[8:6]), .ALU_Out(alu_1_alu_out),
    .sign_flag(alu_1_carry_flag[2]), .zero_flag(alu_1_carry_flag[1]), .carry_flag(alu_1_carry_flag[0]));
  PLA #(.in_width(20), .out_width(19), .\table ("xxx0xxxxxxxxxxxxxxxx 0000000000001111000 # IE=0 (during fetch)\n0xx10000101111111111 0011100000000111000 # jnc opd (Taken)\n1xx10000101111111111 0000000000001111000 # jnc opd (Skip)\n1xx10000110011111111 0011100000000111000 # jc opd (Taken)\n0xx10000110011111111 0000000000001111000 # jc opd (Skip)\nx0x10000110111111111 0011100000000111000 # jnz opd (Taken)\nx1x10000110111111111 0000000000001111000 # jnz opd (Skip)\nx1x10000111011111111 0011100000000111000 # jz opd (Taken)\nx0x10000111011111111 0000000000001111000 # jz opd (Skip)\nxx010000111111111111 0011100000000111000 # jns opd (Taken)\nxx110000111111111111 0000000000001111000 # jns opd (Skip)\nxx110001000011111111 0011100000000111000 # js opd (Taken)\nxx010001000011111111 0000000000001111000 # js opd (Skip)\nxxx10001000111111111 0011100000000111000 # jmp opd\nx1x10001011011111111 0011100000000111000 # je opd (Taken)\nx0x10001011011111111 0000000000001111000 # je opd (Skip)\nx0x10001011111111111 0011100000000111000 # jne opd(Taken)\nx1x10001011111111111 0000000000001111000 # jne opd(Skip)\nx0010001100011111111 0011100000000111000 # ja opd (Taken)\nxxx10001100011111111 0000000000001111000 # ja opd (Skip)\nx0010001100111111111 0011100000000111000 # jae opd (Taken)\nx1010001100111111111 0011100000000111000 # jae opd (Taken)\nxxx10001100111111111 0000000000001111000 # jae opd (Skip)\nx0110001101011111111 0011100000000111000 # jl opd (Taken)\nxxx10001101011111111 0000000000001111000 # jl opd (Skip)\nx0110001101111111111 0011100000000111000 # jle opd (Taken)\nx1010001101111111111 0011100000000111000 # jle opd (Taken)\nxxx10001101111111111 0000000000001111000 # jle opd (Skip)\nxxx10001001111111111 1000000000001111000 # hlt\nxxx10001010011111111 0000000000001111000 # nop\nxxxx1111111111111111 0000000000001111000 # invaild\nxxx10001010111111111 0101000000001010000 # lpc\nxxx10000000000000000 0000010000000000000 # add a, a\nxxx10000000000000001 0000010010000000000 # add a, b\nxxx10000000000000010 0000010100000000000 # add a, c\nxxx10000000000000011 0000010110000000000 # add a, d\nxxx10000000000000100 0000011000000000000 # add a, e\nxxx10000000000000101 0000011010000000000 # add a, bp\nxxx10000000000000110 0000011100000000000 # add a, sp\nxxx10000000000010000 0000110000000001000 # add b, a\nxxx10000000000010001 0000110010000001000 # add b, b\nxxx10000000000010010 0000110100000001000 # add b, c\nxxx10000000000010011 0000110110000001000 # add b, d\nxxx10000000000010100 0000111000000001000 # add b, e\nxxx10000000000010101 0000111010000001000 # add b, bp\nxxx10000000000010110 0000111100000001000 # add b, sp\nxxx10000000000100000 0001010000000010000 # add c, a\nxxx10000000000100001 0001010010000010000 # add c, b\nxxx10000000000100010 0001010100000010000 # add c, c\nxxx10000000000100011 0001010110000010000 # add c, d\nxxx10000000000100100 0001011000000010000 # add c, e\nxxx10000000000100101 0001011010000010000 # add c, bp\nxxx10000000000100110 0001011100000010000 # add c, sp\nxxx10000000000110000 0001110000000011000 # add d, a\nxxx10000000000110001 0001110010000011000 # add d, b\nxxx10000000000110010 0001110100000011000 # add d, c\nxxx10000000000110011 0001110110000011000 # add d, d\nxxx10000000000110100 0001111000000011000 # add d, e\nxxx10000000000110101 0001111010000011000 # add d, bp\nxxx10000000000110110 0001111100000011000 # add d, sp\nxxx10000000001000000 0010010000000100000 # add e, a\nxxx10000000001000001 0010010010000100000 # add e, b\nxxx10000000001000010 0010010100000100000 # add e, c\nxxx10000000001000011 0010010110000100000 # add e, d\nxxx10000000001000100 0010011000000100000 # add e, e\nxxx10000000001000101 0010011010000100000 # add e, bp\nxxx10000000001000110 0010011100000100000 # add e, sp\nxxx10000000001010000 0010110000000101000 # add bp, a\nxxx10000000001010001 0010110010000101000 # add bp, b\nxxx10000000001010010 0010110100000101000 # add bp, c\nxxx10000000001010011 0010110110000101000 # add bp, d\nxxx10000000001010100 0010111000000101000 # add bp, e\nxxx10000000001010101 0010111010000101000 # add bp, bp\nxxx10000000001010110 0010111100000101000 # add bp, sp\nxxx10000000001100000 0011010000000110000 # add sp, a\nxxx10000000001100001 0011010010000110000 # add sp, b\nxxx10000000001100010 0011010100000110000 # add sp, c\nxxx10000000001100011 0011010110000110000 # add sp, d\nxxx10000000001100100 0011011000000110000 # add sp, e\nxxx10000000001100101 0011011010000110000 # add sp, bp\nxxx10000000001100110 0011011100000110000 # add sp, sp\nxxx10000000100000000 0000010000010000000 # sub a, a\nxxx10000000100000001 0000010010010000000 # sub a, b\nxxx10000000100000010 0000010100010000000 # sub a, c\nxxx10000000100000011 0000010110010000000 # sub a, d\nxxx10000000100000100 0000011000010000000 # sub a, e\nxxx10000000100000101 0000011010010000000 # sub a, bp\nxxx10000000100000110 0000011100010000000 # sub a, sp\nxxx10000000100010000 0000110000010001000 # sub b, a\nxxx10000000100010001 0000110010010001000 # sub b, b\nxxx10000000100010010 0000110100010001000 # sub b, c\nxxx10000000100010011 0000110110010001000 # sub b, d\nxxx10000000100010100 0000111000010001000 # sub b, e\nxxx10000000100010101 0000111010010001000 # sub b, bp\nxxx10000000100010110 0000111100010001000 # sub b, sp\nxxx10000000100100000 0001010000010010000 # sub c, a\nxxx10000000100100001 0001010010010010000 # sub c, b\nxxx10000000100100010 0001010100010010000 # sub c, c\nxxx10000000100100011 0001010110010010000 # sub c, d\nxxx10000000100100100 0001011000010010000 # sub c, e\nxxx10000000100100101 0001011010010010000 # sub c, bp\nxxx10000000100100110 0001011100010010000 # sub c, sp\nxxx10000000100110000 0001110000010011000 # sub d, a\nxxx10000000100110001 0001110010010011000 # sub d, b\nxxx10000000100110010 0001110100010011000 # sub d, c\nxxx10000000100110011 0001110110010011000 # sub d, d\nxxx10000000100110100 0001111000010011000 # sub d, e\nxxx10000000100110101 0001111010010011000 # sub d, bp\nxxx10000000100110110 0001111100010011000 # sub d, sp\nxxx10000000101000000 0010010000010100000 # sub e, a\nxxx10000000101000001 0010010010010100000 # sub e, b\nxxx10000000101000010 0010010100010100000 # sub e, c\nxxx10000000101000011 0010010110010100000 # sub e, d\nxxx10000000101000100 0010011000010100000 # sub e, e\nxxx10000000101000101 0010011010010100000 # sub e, bp\nxxx10000000101000110 0010011100010100000 # sub e, sp\nxxx10000000101010000 0010110000010101000 # sub bp, a\nxxx10000000101010001 0010110010010101000 # sub bp, b\nxxx10000000101010010 0010110100010101000 # sub bp, c\nxxx10000000101010011 0010110110010101000 # sub bp, d\nxxx10000000101010100 0010111000010101000 # sub bp, e\nxxx10000000101010101 0010111010010101000 # sub bp, bp\nxxx10000000101010110 0010111100010101000 # sub bp, sp\nxxx10000000101100000 0011010000010110000 # sub sp, a\nxxx10000000101100001 0011010010010110000 # sub sp, b\nxxx10000000101100010 0011010100010110000 # sub sp, c\nxxx10000000101100011 0011010110010110000 # sub sp, d\nxxx10000000101100100 0011011000010110000 # sub sp, e\nxxx10000000101100101 0011011010010110000 # sub sp, bp\nxxx10000000101100110 0011011100010110000 # sub sp, sp\nxxx10000001000000000 0000010000100000000 # mul a, a\nxxx10000001000000001 0000010010100000000 # mul a, b\nxxx10000001000000010 0000010100100000000 # mul a, c\nxxx10000001000000011 0000010110100000000 # mul a, d\nxxx10000001000000100 0000011000100000000 # mul a, e\nxxx10000001000000101 0000011010100000000 # mul a, bp\nxxx10000001000000110 0000011100100000000 # mul a, sp\nxxx10000001000010000 0000110000100001000 # mul b, a\nxxx10000001000010001 0000110010100001000 # mul b, b\nxxx10000001000010010 0000110100100001000 # mul b, c\nxxx10000001000010011 0000110110100001000 # mul b, d\nxxx10000001000010100 0000111000100001000 # mul b, e\nxxx10000001000010101 0000111010100001000 # mul b, bp\nxxx10000001000010110 0000111100100001000 # mul b, sp\nxxx10000001000100000 0001010000100010000 # mul c, a\nxxx10000001000100001 0001010010100010000 # mul c, b\nxxx10000001000100010 0001010100100010000 # mul c, c\nxxx10000001000100011 0001010110100010000 # mul c, d\nxxx10000001000100100 0001011000100010000 # mul c, e\nxxx10000001000100101 0001011010100010000 # mul c, bp\nxxx10000001000100110 0001011100100010000 # mul c, sp\nxxx10000001000110000 0001110000100011000 # mul d, a\nxxx10000001000110001 0001110010100011000 # mul d, b\nxxx10000001000110010 0001110100100011000 # mul d, c\nxxx10000001000110011 0001110110100011000 # mul d, d\nxxx10000001000110100 0001111000100011000 # mul d, e\nxxx10000001000110101 0001111010100011000 # mul d, bp\nxxx10000001000110110 0001111100100011000 # mul d, sp\nxxx10000001001000000 0010010000100100000 # mul e, a\nxxx10000001001000001 0010010010100100000 # mul e, b\nxxx10000001001000010 0010010100100100000 # mul e, c\nxxx10000001001000011 0010010110100100000 # mul e, d\nxxx10000001001000100 0010011000100100000 # mul e, e\nxxx10000001001000101 0010011010100100000 # mul e, bp\nxxx10000001001000110 0010011100100100000 # mul e, sp\nxxx10000001001010000 0010110000100101000 # mul bp, a\nxxx10000001001010001 0010110010100101000 # mul bp, b\nxxx10000001001010010 0010110100100101000 # mul bp, c\nxxx10000001001010011 0010110110100101000 # mul bp, d\nxxx10000001001010100 0010111000100101000 # mul bp, e\nxxx10000001001010101 0010111010100101000 # mul bp, bp\nxxx10000001001010110 0010111100100101000 # mul bp, sp\nxxx10000001001100000 0011010000100110000 # mul sp, a\nxxx10000001001100001 0011010010100110000 # mul sp, b\nxxx10000001001100010 0011010100100110000 # mul sp, c\nxxx10000001001100011 0011010110100110000 # mul sp, d\nxxx10000001001100100 0011011000100110000 # mul sp, e\nxxx10000001001100101 0011011010100110000 # mul sp, bp\nxxx10000001001100110 0011011100100110000 # mul sp, sp\nxxx10000001100000000 0000010000110000000 # and a, a\nxxx10000001100000001 0000010010110000000 # and a, b\nxxx10000001100000010 0000010100110000000 # and a, c\nxxx10000001100000011 0000010110110000000 # and a, d\nxxx10000001100000100 0000011000110000000 # and a, e\nxxx10000001100000101 0000011010110000000 # and a, bp\nxxx10000001100000110 0000011100110000000 # and a, sp\nxxx10000001100010000 0000110000110001000 # and b, a\nxxx10000001100010001 0000110010110001000 # and b, b\nxxx10000001100010010 0000110100110001000 # and b, c\nxxx10000001100010011 0000110110110001000 # and b, d\nxxx10000001100010100 0000111000110001000 # and b, e\nxxx10000001100010101 0000111010110001000 # and b, bp\nxxx10000001100010110 0000111100110001000 # and b, sp\nxxx10000001100100000 0001010000110010000 # and c, a\nxxx10000001100100001 0001010010110010000 # and c, b\nxxx10000001100100010 0001010100110010000 # and c, c\nxxx10000001100100011 0001010110110010000 # and c, d\nxxx10000001100100100 0001011000110010000 # and c, e\nxxx10000001100100101 0001011010110010000 # and c, bp\nxxx10000001100100110 0001011100110010000 # and c, sp\nxxx10000001100110000 0001110000110011000 # and d, a\nxxx10000001100110001 0001110010110011000 # and d, b\nxxx10000001100110010 0001110100110011000 # and d, c\nxxx10000001100110011 0001110110110011000 # and d, d\nxxx10000001100110100 0001111000110011000 # and d, e\nxxx10000001100110101 0001111010110011000 # and d, bp\nxxx10000001100110110 0001111100110011000 # and d, sp\nxxx10000001101000000 0010010000110100000 # and e, a\nxxx10000001101000001 0010010010110100000 # and e, b\nxxx10000001101000010 0010010100110100000 # and e, c\nxxx10000001101000011 0010010110110100000 # and e, d\nxxx10000001101000100 0010011000110100000 # and e, e\nxxx10000001101000101 0010011010110100000 # and e, bp\nxxx10000001101000110 0010011100110100000 # and e, sp\nxxx10000001101010000 0010110000110101000 # and bp, a\nxxx10000001101010001 0010110010110101000 # and bp, b\nxxx10000001101010010 0010110100110101000 # and bp, c\nxxx10000001101010011 0010110110110101000 # and bp, d\nxxx10000001101010100 0010111000110101000 # and bp, e\nxxx10000001101010101 0010111010110101000 # and bp, bp\nxxx10000001101010110 0010111100110101000 # and bp, sp\nxxx10000001101100000 0011010000110110000 # and sp, a\nxxx10000001101100001 0011010010110110000 # and sp, b\nxxx10000001101100010 0011010100110110000 # and sp, c\nxxx10000001101100011 0011010110110110000 # and sp, d\nxxx10000001101100100 0011011000110110000 # and sp, e\nxxx10000001101100101 0011011010110110000 # and sp, bp\nxxx10000001101100110 0011011100110110000 # and sp, sp\nxxx10000010000000000 0000010001000000000 # or a, a\nxxx10000010000000001 0000010011000000000 # or a, b\nxxx10000010000000010 0000010101000000000 # or a, c\nxxx10000010000000011 0000010111000000000 # or a, d\nxxx10000010000000100 0000011001000000000 # or a, e\nxxx10000010000000101 0000011011000000000 # or a, bp\nxxx10000010000000110 0000011101000000000 # or a, sp\nxxx10000010000010000 0000110001000001000 # or b, a\nxxx10000010000010001 0000110011000001000 # or b, b\nxxx10000010000010010 0000110101000001000 # or b, c\nxxx10000010000010011 0000110111000001000 # or b, d\nxxx10000010000010100 0000111001000001000 # or b, e\nxxx10000010000010101 0000111011000001000 # or b, bp\nxxx10000010000010110 0000111101000001000 # or b, sp\nxxx10000010000100000 0001010001000010000 # or c, a\nxxx10000010000100001 0001010011000010000 # or c, b\nxxx10000010000100010 0001010101000010000 # or c, c\nxxx10000010000100011 0001010111000010000 # or c, d\nxxx10000010000100100 0001011001000010000 # or c, e\nxxx10000010000100101 0001011011000010000 # or c, bp\nxxx10000010000100110 0001011101000010000 # or c, sp\nxxx10000010000110000 0001110001000011000 # or d, a\nxxx10000010000110001 0001110011000011000 # or d, b\nxxx10000010000110010 0001110101000011000 # or d, c\nxxx10000010000110011 0001110111000011000 # or d, d\nxxx10000010000110100 0001111001000011000 # or d, e\nxxx10000010000110101 0001111011000011000 # or d, bp\nxxx10000010000110110 0001111101000011000 # or d, sp\nxxx10000010001000000 0010010001000100000 # or e, a\nxxx10000010001000001 0010010011000100000 # or e, b\nxxx10000010001000010 0010010101000100000 # or e, c\nxxx10000010001000011 0010010111000100000 # or e, d\nxxx10000010001000100 0010011001000100000 # or e, e\nxxx10000010001000101 0010011011000100000 # or e, bp\nxxx10000010001000110 0010011101000100000 # or e, sp\nxxx10000010001010000 0010110001000101000 # or bp, a\nxxx10000010001010001 0010110011000101000 # or bp, b\nxxx10000010001010010 0010110101000101000 # or bp, c\nxxx10000010001010011 0010110111000101000 # or bp, d\nxxx10000010001010100 0010111001000101000 # or bp, e\nxxx10000010001010101 0010111011000101000 # or bp, bp\nxxx10000010001010110 0010111101000101000 # or bp, sp\nxxx10000010001100000 0011010001000110000 # or sp, a\nxxx10000010001100001 0011010011000110000 # or sp, b\nxxx10000010001100010 0011010101000110000 # or sp, c\nxxx10000010001100011 0011010111000110000 # or sp, d\nxxx10000010001100100 0011011001000110000 # or sp, e\nxxx10000010001100101 0011011011000110000 # or sp, bp\nxxx10000010001100110 0011011101000110000 # or sp, sp\nxxx10000011000000000 0000010001100000000 # xor a, a\nxxx10000011000000001 0000010011100000000 # xor a, b\nxxx10000011000000010 0000010101100000000 # xor a, c\nxxx10000011000000011 0000010111100000000 # xor a, d\nxxx10000011000000100 0000011001100000000 # xor a, e\nxxx10000011000000101 0000011011100000000 # xor a, bp\nxxx10000011000000110 0000011101100000000 # xor a, sp\nxxx10000011000010000 0000110001100001000 # xor b, a\nxxx10000011000010001 0000110011100001000 # xor b, b\nxxx10000011000010010 0000110101100001000 # xor b, c\nxxx10000011000010011 0000110111100001000 # xor b, d\nxxx10000011000010100 0000111001100001000 # xor b, e\nxxx10000011000010101 0000111011100001000 # xor b, bp\nxxx10000011000010110 0000111101100001000 # xor b, sp\nxxx10000011000100000 0001010001100010000 # xor c, a\nxxx10000011000100001 0001010011100010000 # xor c, b\nxxx10000011000100010 0001010101100010000 # xor c, c\nxxx10000011000100011 0001010111100010000 # xor c, d\nxxx10000011000100100 0001011001100010000 # xor c, e\nxxx10000011000100101 0001011011100010000 # xor c, bp\nxxx10000011000100110 0001011101100010000 # xor c, sp\nxxx10000011000110000 0001110001100011000 # xor d, a\nxxx10000011000110001 0001110011100011000 # xor d, b\nxxx10000011000110010 0001110101100011000 # xor d, c\nxxx10000011000110011 0001110111100011000 # xor d, d\nxxx10000011000110100 0001111001100011000 # xor d, e\nxxx10000011000110101 0001111011100011000 # xor d, bp\nxxx10000011000110110 0001111101100011000 # xor d, sp\nxxx10000011001000000 0010010001100100000 # xor e, a\nxxx10000011001000001 0010010011100100000 # xor e, b\nxxx10000011001000010 0010010101100100000 # xor e, c\nxxx10000011001000011 0010010111100100000 # xor e, d\nxxx10000011001000100 0010011001100100000 # xor e, e\nxxx10000011001000101 0010011011100100000 # xor e, bp\nxxx10000011001000110 0010011101100100000 # xor e, sp\nxxx10000011001010000 0010110001100101000 # xor bp, a\nxxx10000011001010001 0010110011100101000 # xor bp, b\nxxx10000011001010010 0010110101100101000 # xor bp, c\nxxx10000011001010011 0010110111100101000 # xor bp, d\nxxx10000011001010100 0010111001100101000 # xor bp, e\nxxx10000011001010101 0010111011100101000 # xor bp, bp\nxxx10000011001010110 0010111101100101000 # xor bp, sp\nxxx10000011001100000 0011010001100110000 # xor sp, a\nxxx10000011001100001 0011010011100110000 # xor sp, b\nxxx10000011001100010 0011010101100110000 # xor sp, c\nxxx10000011001100011 0011010111100110000 # xor sp, d\nxxx10000011001100100 0011011001100110000 # xor sp, e\nxxx10000011001100101 0011011011100110000 # xor sp, bp\nxxx10000011001100110 0011011101100110000 # xor sp, sp\nxxx10000011100000000 0000010001110000000 # shr a, a\nxxx10000011100000001 0000010011110000000 # shr a, b\nxxx10000011100000010 0000010101110000000 # shr a, c\nxxx10000011100000011 0000010111110000000 # shr a, d\nxxx10000011100000100 0000011001110000000 # shr a, e\nxxx10000011100000101 0000011011110000000 # shr a, bp\nxxx10000011100000110 0000011101110000000 # shr a, sp\nxxx10000011100010000 0000110001110001000 # shr b, a\nxxx10000011100010001 0000110011110001000 # shr b, b\nxxx10000011100010010 0000110101110001000 # shr b, c\nxxx10000011100010011 0000110111110001000 # shr b, d\nxxx10000011100010100 0000111001110001000 # shr b, e\nxxx10000011100010101 0000111011110001000 # shr b, bp\nxxx10000011100010110 0000111101110001000 # shr b, sp\nxxx10000011100100000 0001010001110010000 # shr c, a\nxxx10000011100100001 0001010011110010000 # shr c, b\nxxx10000011100100010 0001010101110010000 # shr c, c\nxxx10000011100100011 0001010111110010000 # shr c, d\nxxx10000011100100100 0001011001110010000 # shr c, e\nxxx10000011100100101 0001011011110010000 # shr c, bp\nxxx10000011100100110 0001011101110010000 # shr c, sp\nxxx10000011100110000 0001110001110011000 # shr d, a\nxxx10000011100110001 0001110011110011000 # shr d, b\nxxx10000011100110010 0001110101110011000 # shr d, c\nxxx10000011100110011 0001110111110011000 # shr d, d\nxxx10000011100110100 0001111001110011000 # shr d, e\nxxx10000011100110101 0001111011110011000 # shr d, bp\nxxx10000011100110110 0001111101110011000 # shr d, sp\nxxx10000011101000000 0010010001110100000 # shr e, a\nxxx10000011101000001 0010010011110100000 # shr e, b\nxxx10000011101000010 0010010101110100000 # shr e, c\nxxx10000011101000011 0010010111110100000 # shr e, d\nxxx10000011101000100 0010011001110100000 # shr e, e\nxxx10000011101000101 0010011011110100000 # shr e, bp\nxxx10000011101000110 0010011101110100000 # shr e, sp\nxxx10000011101010000 0010110001110101000 # shr bp, a\nxxx10000011101010001 0010110011110101000 # shr bp, b\nxxx10000011101010010 0010110101110101000 # shr bp, c\nxxx10000011101010011 0010110111110101000 # shr bp, d\nxxx10000011101010100 0010111001110101000 # shr bp, e\nxxx10000011101010101 0010111011110101000 # shr bp, bp\nxxx10000011101010110 0010111101110101000 # shr bp, sp\nxxx10000011101100000 0011010001110110000 # shr sp, a\nxxx10000011101100001 0011010011110110000 # shr sp, b\nxxx10000011101100010 0011010101110110000 # shr sp, c\nxxx10000011101100011 0011010111110110000 # shr sp, d\nxxx10000011101100100 0011011001110110000 # shr sp, e\nxxx10000011101100101 0011011011110110000 # shr sp, bp\nxxx10000011101100110 0011011101110110000 # shr sp, sp\nxxx10000000000001111 0000011110000000000 # add a, opd\nxxx10000000000011111 0000111110000001000 # add b, opd\nxxx10000000000101111 0001011110000010000 # add c, opd\nxxx10000000000111111 0001111110000011000 # add d, opd\nxxx10000000001001111 0010011110000100000 # add e, opd\nxxx10000000001011111 0010111110000101000 # add bp, opd\nxxx10000000001101111 0011011110000110000 # add sp, opd\nxxx10000000100001111 0000011110010000000 # sub a, opd\nxxx10000000100011111 0000111110010001000 # sub b, opd\nxxx10000000100101111 0001011110010010000 # sub c, opd\nxxx10000000100111111 0001111110010011000 # sub d, opd\nxxx10000000101001111 0010011110010100000 # sub e, opd\nxxx10000000101011111 0010111110010101000 # sub bp, opd\nxxx10000000101101111 0011011110010110000 # sub sp, opd\nxxx10000001000001111 0000011110100000000 # mul a, opd\nxxx10000001000011111 0000111110100001000 # mul b, opd\nxxx10000001000101111 0001011110100010000 # mul c, opd\nxxx10000001000111111 0001111110100011000 # mul d, opd\nxxx10000001001001111 0010011110100100000 # mul e, opd\nxxx10000001001011111 0010111110100101000 # mul bp, opd\nxxx10000001001101111 0011011110100110000 # mul sp, opd\nxxx10000001100001111 0000011110110000000 # and a, opd\nxxx10000001100011111 0000111110110001000 # and b, opd\nxxx10000001100101111 0001011110110010000 # and c, opd\nxxx10000001100111111 0001111110110011000 # and d, opd\nxxx10000001101001111 0010011110110100000 # and e, opd\nxxx10000001101011111 0010111110110101000 # and bp, opd\nxxx10000001101101111 0011011110110110000 # and sp, opd\nxxx10000010000001111 0000011111000000000 # or a, opd\nxxx10000010000011111 0000111111000001000 # or b, opd\nxxx10000010000101111 0001011111000010000 # or c, opd\nxxx10000010000111111 0001111111000011000 # or d, opd\nxxx10000010001001111 0010011111000100000 # or e, opd\nxxx10000010001011111 0010111111000101000 # or bp, opd\nxxx10000010001101111 0011011111000110000 # or sp, opd\nxxx10000011000001111 0000011111100000000 # xor a, opd\nxxx10000011000011111 0000111111100001000 # xor b, opd\nxxx10000011000101111 0001011111100010000 # xor c, opd\nxxx10000011000111111 0001111111100011000 # xor d, opd\nxxx10000011001001111 0010011111100100000 # xor e, opd\nxxx10000011001011111 0010111111100101000 # xor bp, opd\nxxx10000011001101111 0011011111100110000 # xor sp, opd\nxxx10000011100001111 0000011111110000000 # shr a, opd\nxxx10000011100011111 0000111111110001000 # shr b, opd\nxxx10000011100101111 0001011111110010000 # shr c, opd\nxxx10000011100111111 0001111111110011000 # shr d, opd\nxxx10000011101001111 0010011111110100000 # shr e, opd\nxxx10000011101011111 0010111111110101000 # shr bp, opd\nxxx10000011101101111 0011011111110110000 # shr sp, opd\nxxx10000000000001001 0100110000000000010 # add a, [memaddr+opd]\nxxx10000000000011001 0100110010000001010 # add b, [memaddr+opd]\nxxx10000000000101001 0100110100000010010 # add c, [memaddr+opd]\nxxx10000000000111001 0100110110000011010 # add d, [memaddr+opd]\nxxx10000000001001001 0100111000000100010 # add e, [memaddr+opd]\nxxx10000000001011001 0100111010000101010 # add bp, [memaddr+opd]\nxxx10000000001101001 0100111100000110010 # add sp, [memaddr+opd]\nxxx10000000100001001 0100110000010000010 # sub a, [memaddr+opd]\nxxx10000000100011001 0100110010010001010 # sub b, [memaddr+opd]\nxxx10000000100101001 0100110100010010010 # sub c, [memaddr+opd]\nxxx10000000100111001 0100110110010011010 # sub d, [memaddr+opd]\nxxx10000000101001001 0100111000010100010 # sub e, [memaddr+opd]\nxxx10000000101011001 0100111010010101010 # sub bp, [memaddr+opd]\nxxx10000000101101001 0100111100010110010 # sub sp, [memaddr+opd]\nxxx10000001000001001 0100110000100000010 # mul a, [memaddr+opd]\nxxx10000001000011001 0100110010100001010 # mul b, [memaddr+opd]\nxxx10000001000101001 0100110100100010010 # mul c, [memaddr+opd]\nxxx10000001000111001 0100110110100011010 # mul d, [memaddr+opd]\nxxx10000001001001001 0100111000100100010 # mul e, [memaddr+opd]\nxxx10000001001011001 0100111010100101010 # mul bp, [memaddr+opd]\nxxx10000001001101001 0100111100100110010 # mul sp, [memaddr+opd]\nxxx10000001100001001 0100110000110000010 # and a, [memaddr+opd]\nxxx10000001100011001 0100110010110001010 # and b, [memaddr+opd]\nxxx10000001100101001 0100110100110010010 # and c, [memaddr+opd]\nxxx10000001100111001 0100110110110011010 # and d, [memaddr+opd]\nxxx10000001101001001 0100111000110100010 # and e, [memaddr+opd]\nxxx10000001101011001 0100111010110101010 # and bp, [memaddr+opd]\nxxx10000001101101001 0100111100110110010 # and sp, [memaddr+opd]\nxxx10000010000001001 0100110001000000010 # or a, [memaddr+opd]\nxxx10000010000011001 0100110011000001010 # or b, [memaddr+opd]\nxxx10000010000101001 0100110101000010010 # or c, [memaddr+opd]\nxxx10000010000111001 0100110111000011010 # or d, [memaddr+opd]\nxxx10000010001001001 0100111001000100010 # or e, [memaddr+opd]\nxxx10000010001011001 0100111011000101010 # or bp, [memaddr+opd]\nxxx10000010001101001 0100111101000110010 # or sp, [memaddr+opd]\nxxx10000011000001001 0100110001100000010 # xor a, [memaddr+opd]\nxxx10000011000011001 0100110011100001010 # xor b, [memaddr+opd]\nxxx10000011000101001 0100110101100010010 # xor c, [memaddr+opd]\nxxx10000011000111001 0100110111100011010 # xor d, [memaddr+opd]\nxxx10000011001001001 0100111001100100010 # xor e, [memaddr+opd]\nxxx10000011001011001 0100111011100101010 # xor bp, [memaddr+opd]\nxxx10000011001101001 0100111101100110010 # xor sp, [memaddr+opd]\nxxx10000011100001001 0100110001110000010 # shr a, [memaddr+opd]\nxxx10000011100011001 0100110011110001010 # shr b, [memaddr+opd]\nxxx10000011100101001 0100110101110010010 # shr c, [memaddr+opd]\nxxx10000011100111001 0100110111110011010 # shr d, [memaddr+opd]\nxxx10000011101001001 0100111001110100010 # shr e, [memaddr+opd]\nxxx10000011101011001 0100111011110101010 # shr bp, [memaddr+opd]\nxxx10000011101101001 0100111101110110010 # shr sp, [memaddr+opd]\nxxx10000000010111111 0101111110001010000 # add memval,opd\nxxx10000010100001111 0000010001010000000 # not a\nxxx10000010100011111 0000110001010001000 # not b\nxxx10000010100101111 0001010001010010000 # not c\nxxx10000010100111111 0001110001010011000 # not d\nxxx10000010101001111 0010010001010100000 # not e\nxxx10000010101011111 0010110001010101000 # not bp\nxxx10000010101101111 0011010001010110000 # not sp\nxxx10000100000000000 0000000000000000000 # mov a, a\nxxx10000100000000001 0000100000000000000 # mov a, b\nxxx10000100000000010 0001000000000000000 # mov a, c\nxxx10000100000000011 0001100000000000000 # mov a, d\nxxx10000100000000100 0010000000000000000 # mov a, e\nxxx10000100000000101 0010100000000000000 # mov a, bp\nxxx10000100000000110 0011000000000000000 # mov a, sp\nxxx10000100000010000 0000000000000001000 # mov b, a\nxxx10000100000010001 0000100000000001000 # mov b, b\nxxx10000100000010010 0001000000000001000 # mov b, c\nxxx10000100000010011 0001100000000001000 # mov b, d\nxxx10000100000010100 0010000000000001000 # mov b, e\nxxx10000100000010101 0010100000000001000 # mov b, bp\nxxx10000100000010110 0011000000000001000 # mov b, sp\nxxx10000100000100000 0000000000000010000 # mov c, a\nxxx10000100000100001 0000100000000010000 # mov c, b\nxxx10000100000100010 0001000000000010000 # mov c, c\nxxx10000100000100011 0001100000000010000 # mov c, d\nxxx10000100000100100 0010000000000010000 # mov c, e\nxxx10000100000100101 0010100000000010000 # mov c, bp\nxxx10000100000100110 0011000000000010000 # mov c, sp\nxxx10000100000110000 0000000000000011000 # mov d, a\nxxx10000100000110001 0000100000000011000 # mov d, b\nxxx10000100000110010 0001000000000011000 # mov d, c\nxxx10000100000110011 0001100000000011000 # mov d, d\nxxx10000100000110100 0010000000000011000 # mov d, e\nxxx10000100000110101 0010100000000011000 # mov d, bp\nxxx10000100000110110 0011000000000011000 # mov d, sp\nxxx10000100001000000 0000000000000100000 # mov e, a\nxxx10000100001000001 0000100000000100000 # mov e, b\nxxx10000100001000010 0001000000000100000 # mov e, c\nxxx10000100001000011 0001100000000100000 # mov e, d\nxxx10000100001000100 0010000000000100000 # mov e, e\nxxx10000100001000101 0010100000000100000 # mov e, bp\nxxx10000100001000110 0011000000000100000 # mov e, sp\nxxx10000100001010000 0000000000000101000 # mov bp, a\nxxx10000100001010001 0000100000000101000 # mov bp, b\nxxx10000100001010010 0001000000000101000 # mov bp, c\nxxx10000100001010011 0001100000000101000 # mov bp, d\nxxx10000100001010100 0010000000000101000 # mov bp, e\nxxx10000100001010101 0010100000000101000 # mov bp, bp\nxxx10000100001010110 0011000000000101000 # mov bp, sp\nxxx10000100001100000 0000000000000110000 # mov sp, a\nxxx10000100001100001 0000100000000110000 # mov sp, b\nxxx10000100001100010 0001000000000110000 # mov sp, c\nxxx10000100001100011 0001100000000110000 # mov sp, d\nxxx10000100001100100 0010000000000110000 # mov sp, e\nxxx10000100001100101 0010100000000110000 # mov sp, bp\nxxx10000100001100110 0011000000000110000 # mov sp, sp\nxxx10000100000001001 0100100000000000010 # mov a, [memaddr+opd]\nxxx10000100000011001 0100100000000001010 # mov b, [memaddr+opd]\nxxx10000100000101001 0100100000000010010 # mov c, [memaddr+opd]\nxxx10000100000111001 0100100000000011010 # mov d, [memaddr+opd]\nxxx10000100001001001 0100100000000100010 # mov e, [memaddr+opd]\nxxx10000100001011001 0100100000000101010 # mov bp, [memaddr+opd]\nxxx10000100001101001 0100100000000110010 # mov sp, [memaddr+opd]\nxxx10000100010111001 0100100000001010010 # mov memval, [memaddr+opd]\nxxx10000100010100000 0000000000001001000 # mov memaddr,a\nxxx10000100010100001 0000100000001001000 # mov memaddr,b\nxxx10000100010100010 0001000000001001000 # mov memaddr,c\nxxx10000100010100011 0001100000001001000 # mov memaddr,d\nxxx10000100010100100 0010000000001001000 # mov memaddr,e\nxxx10000100010100101 0010100000001001000 # mov memaddr,bp\nxxx10000100010100110 0011000000001001000 # mov memaddr,sp\nxxx10000100010110000 0000000000001010000 # mov memval,a\nxxx10000100010110001 0000100000001010000 # mov memval,b\nxxx10000100010110010 0001000000001010000 # mov memval,c\nxxx10000100010110011 0001100000001010000 # mov memval,d\nxxx10000100010110100 0010000000001010000 # mov memval,e\nxxx10000100010110101 0010100000001010000 # mov memval,bp\nxxx10000100010110110 0011000000001010000 # mov memval,sp\nxxx10000100010101010 0000000000001111011 # mov [memaddr+opd],memval\nxxx10000100010101111 0011100000001001000 # mov memaddr, opd\nxxx10000100010111111 0011100000001010000 # mov memval, opd\nxxx10000100000001111 0011100000000000000 # mov a, opd\nxxx10000100000011111 0011100000000001000 # mov b, opd\nxxx10000100000101111 0011100000000010000 # mov c, opd\nxxx10000100000111111 0011100000000011000 # mov d, opd\nxxx10000100001001111 0011100000000100000 # mov e, opd\nxxx10000100001011111 0011100000000101000 # mov bp, opd\nxxx10000100001101111 0011100000000110000 # mov sp, opd\nxxx10000100100001111 0100000000000000000 # in a\nxxx10000100100011111 0100000000000001000 # in b\nxxx10000100100101111 0100000000000010000 # in c\nxxx10000100100111111 0100000000000011000 # in d\nxxx10000100101001111 0100000000000100000 # in e\nxxx10000100101011111 0100000000000101000 # in bp\nxxx10000100101101111 0100000000000110000 # in sp\nxxx10000101000001111 0000000000001000000 # out a\nxxx10000101000011111 0000100000001000000 # out b\nxxx10000101000101111 0001000000001000000 # out c\nxxx10000101000111111 0001100000001000000 # out d\nxxx10000101001001111 0010000000001000000 # out e\nxxx10000101001011111 0010100000001000000 # out bp\nxxx10000101001101111 0011000000001000000 # out sp\nxxx10000101011111111 0011100000001000000 # out opd\nxxx10001001000000000 0000010000011111000 # cmp a, a\nxxx10001001000000001 0000010010011111000 # cmp a, b\nxxx10001001000000010 0000010100011111000 # cmp a, c\nxxx10001001000000011 0000010110011111000 # cmp a, d\nxxx10001001000000100 0000011000011111000 # cmp a, e\nxxx10001001000000101 0000011010011111000 # cmp a, bp\nxxx10001001000000110 0000011100011111000 # cmp a, sp\nxxx10001001000010000 0000110000011111000 # cmp b, a\nxxx10001001000010001 0000110010011111000 # cmp b, b\nxxx10001001000010010 0000110100011111000 # cmp b, c\nxxx10001001000010011 0000110110011111000 # cmp b, d\nxxx10001001000010100 0000111000011111000 # cmp b, e\nxxx10001001000010101 0000111010011111000 # cmp b, bp\nxxx10001001000010110 0000111100011111000 # cmp b, sp\nxxx10001001000100000 0001010000011111000 # cmp c, a\nxxx10001001000100001 0001010010011111000 # cmp c, b\nxxx10001001000100010 0001010100011111000 # cmp c, c\nxxx10001001000100011 0001010110011111000 # cmp c, d\nxxx10001001000100100 0001011000011111000 # cmp c, e\nxxx10001001000100101 0001011010011111000 # cmp c, bp\nxxx10001001000100110 0001011100011111000 # cmp c, sp\nxxx10001001000110000 0001110000011111000 # cmp d, a\nxxx10001001000110001 0001110010011111000 # cmp d, b\nxxx10001001000110010 0001110100011111000 # cmp d, c\nxxx10001001000110011 0001110110011111000 # cmp d, d\nxxx10001001000110100 0001111000011111000 # cmp d, e\nxxx10001001000110101 0001111010011111000 # cmp d, bp\nxxx10001001000110110 0001111100011111000 # cmp d, sp\nxxx10001001001000000 0010010000011111000 # cmp e, a\nxxx10001001001000001 0010010010011111000 # cmp e, b\nxxx10001001001000010 0010010100011111000 # cmp e, c\nxxx10001001001000011 0010010110011111000 # cmp e, d\nxxx10001001001000100 0010011000011111000 # cmp e, e\nxxx10001001001000101 0010011010011111000 # cmp e, bp\nxxx10001001001000110 0010011100011111000 # cmp e, sp\nxxx10001001001010000 0010110000011111000 # cmp bp, a\nxxx10001001001010001 0010110010011111000 # cmp bp, b\nxxx10001001001010010 0010110100011111000 # cmp bp, c\nxxx10001001001010011 0010110110011111000 # cmp bp, d\nxxx10001001001010100 0010111000011111000 # cmp bp, e\nxxx10001001001010101 0010111010011111000 # cmp bp, bp\nxxx10001001001010110 0010111100011111000 # cmp bp, sp\nxxx10001001001100000 0011010000011111000 # cmp sp, a\nxxx10001001001100001 0011010010011111000 # cmp sp, b\nxxx10001001001100010 0011010100011111000 # cmp sp, c\nxxx10001001001100011 0011010110011111000 # cmp sp, d\nxxx10001001001100100 0011011000011111000 # cmp sp, e\nxxx10001001001100101 0011011010011111000 # cmp sp, bp\nxxx10001001001100110 0011011100011111000 # cmp sp, sp\nxxx10001001000001111 0000011110011111000 # cmp a, opd\nxxx10001001000011111 0000111110011111000 # cmp b, opd\nxxx10001001000101111 0001011110011111000 # cmp c, opd\nxxx10001001000111111 0001111110011111000 # cmp d, opd\nxxx10001001001001111 0010011110011111000 # cmp e, opd\nxxx10001001001011111 0010111110011111000 # cmp bp, opd\nxxx10001001001101111 0011011110011111000 # cmp sp, opd\nxxx10001000110111111 0101100000000111000 # jmp memval\n0xx10000101100001111 0000000000000111000 # jnc a (Taken)\n0xx10000101100011111 0000100000000111000 # jnc b (Taken)\n0xx10000101100101111 0001000000000111000 # jnc c (Taken)\n0xx10000101100111111 0001100000000111000 # jnc d (Taken)\n0xx10000101101001111 0010000000000111000 # jnc e (Taken)\n0xx10000101101011111 0010100000000111000 # jnc bp (Taken)\n0xx10000101101101111 0011000000000111000 # jnc sp (Taken)\n1xx10000101100001111 0000000000001111000 # jnc a (Skip)\n1xx10000101100011111 0000000000001111000 # jnc b (Skip)\n1xx10000101100101111 0000000000001111000 # jnc c (Skip)\n1xx10000101100111111 0000000000001111000 # jnc d (Skip)\n1xx10000101101001111 0000000000001111000 # jnc e (Skip)\n1xx10000101101011111 0000000000001111000 # jnc bp (Skip)\n1xx10000101101101111 0000000000001111000 # jnc sp (Skip)\n1xx10000110000001111 0000000000000111000 # jc a (Taken)\n1xx10000110000011111 0000100000000111000 # jc b (Taken)\n1xx10000110000101111 0001000000000111000 # jc c (Taken)\n1xx10000110000111111 0001100000000111000 # jc d (Taken)\n1xx10000110001001111 0010000000000111000 # jc e (Taken)\n1xx10000110001011111 0010100000000111000 # jc bp (Taken)\n1xx10000110001101111 0011000000000111000 # jc sp (Taken)\n0xx10000110000001111 0000000000001111000 # jc a (Skip)\n0xx10000110000011111 0000000000001111000 # jc b (Skip)\n0xx10000110000101111 0000000000001111000 # jc c (Skip)\n0xx10000110000111111 0000000000001111000 # jc d (Skip)\n0xx10000110001001111 0000000000001111000 # jc e (Skip)\n0xx10000110001011111 0000000000001111000 # jc bp (Skip)\n0xx10000110001101111 0000000000001111000 # jc sp (Skip)\nx0x10000110100001111 0000000000000111000 # jnz a (Taken)\nx0x10000110100011111 0000100000000111000 # jnz b (Taken)\nx0x10000110100101111 0001000000000111000 # jnz c (Taken)\nx0x10000110100111111 0001100000000111000 # jnz d (Taken)\nx0x10000110101001111 0010000000000111000 # jnz e (Taken)\nx0x10000110101011111 0010100000000111000 # jnz bp (Taken)\nx0x10000110101101111 0011000000000111000 # jnz sp (Taken)\nx1x10000110100001111 0000000000001111000 # jnz a (Skip)\nx1x10000110100011111 0000000000001111000 # jnz b (Skip)\nx1x10000110100101111 0000000000001111000 # jnz c (Skip)\nx1x10000110100111111 0000000000001111000 # jnz d (Skip)\nx1x10000110101001111 0000000000001111000 # jnz e (Skip)\nx1x10000110101011111 0000000000001111000 # jnz bp (Skip)\nx1x10000110101101111 0000000000001111000 # jnz sp (Skip)\nx1x10000111000001111 0000000000000111000 # jz a (Taken)\nx1x10000111000011111 0000100000000111000 # jz b (Taken)\nx1x10000111000101111 0001000000000111000 # jz c (Taken)\nx1x10000111000111111 0001100000000111000 # jz d (Taken)\nx1x10000111001001111 0010000000000111000 # jz e (Taken)\nx1x10000111001011111 0010100000000111000 # jz bp (Taken)\nx1x10000111001101111 0011000000000111000 # jz sp (Taken)\nx0x10000111000001111 0000000000001111000 # jz a (Skip)\nx0x10000111000011111 0000000000001111000 # jz b (Skip)\nx0x10000111000101111 0000000000001111000 # jz c (Skip)\nx0x10000111000111111 0000000000001111000 # jz d (Skip)\nx0x10000111001001111 0000000000001111000 # jz e (Skip)\nx0x10000111001011111 0000000000001111000 # jz bp (Skip)\nx0x10000111001101111 0000000000001111000 # jz sp (Skip)\nxx010000111100001111 0000000000000111000 # jns a (Taken)\nxx010000111100011111 0000100000000111000 # jns b (Taken)\nxx010000111100101111 0001000000000111000 # jns c (Taken)\nxx010000111100111111 0001100000000111000 # jns d (Taken)\nxx010000111101001111 0010000000000111000 # jns e (Taken)\nxx010000111101011111 0010100000000111000 # jns bp (Taken)\nxx010000111101101111 0011000000000111000 # jns sp (Taken)\nxx110000111100001111 0000000000001111000 # jns a (Skip)\nxx110000111100011111 0000000000001111000 # jns b (Skip)\nxx110000111100101111 0000000000001111000 # jns c (Skip)\nxx110000111100111111 0000000000001111000 # jns d (Skip)\nxx110000111101001111 0000000000001111000 # jns e (Skip)\nxx110000111101011111 0000000000001111000 # jns bp (Skip)\nxx110000111101101111 0000000000001111000 # jns sp (Skip)\nxx110001000000001111 0000000000000111000 # js a (Taken)\nxx110001000000011111 0000100000000111000 # js b (Taken)\nxx110001000000101111 0001000000000111000 # js c (Taken)\nxx110001000000111111 0001100000000111000 # js d (Taken)\nxx110001000001001111 0010000000000111000 # js e (Taken)\nxx110001000001011111 0010100000000111000 # js bp (Taken)\nxx110001000001101111 0011000000000111000 # js sp (Taken)\nxx010001000000001111 0000000000001111000 # js a (Skip)\nxx010001000000011111 0000000000001111000 # js b (Skip)\nxx010001000000101111 0000000000001111000 # js c (Skip)\nxx010001000000111111 0000000000001111000 # js d (Skip)\nxx010001000001001111 0000000000001111000 # js e (Skip)\nxx010001000001011111 0000000000001111000 # js bp (Skip)\nxx010001000001101111 0000000000001111000 # js sp (Skip)\nxxx10001000100001111 0000000000000111000 # jmp a\nxxx10001000100011111 0000100000000111000 # jmp b\nxxx10001000100101111 0001000000000111000 # jmp c\nxxx10001000100111111 0001100000000111000 # jmp d\nxxx10001000101001111 0010000000000111000 # jmp e\nxxx10001000101011111 0010100000000111000 # jmp bp\nxxx10001000101101111 0011000000000111000 # jmp sp\nx1x10001011000001111 0000000000000111000 # je a (Taken)\nx1x10001011000011111 0000100000000111000 # je b (Taken)\nx1x10001011000101111 0001000000000111000 # je c (Taken)\nx1x10001011000111111 0001100000000111000 # je d (Taken)\nx1x10001011001001111 0010000000000111000 # je e (Taken)\nx1x10001011001011111 0010100000000111000 # je bp (Taken)\nx1x10001011001101111 0011000000000111000 # je sp (Taken)\nx0x10001011000001111 0000000000001111000 # je a (Skip)\nx0x10001011000011111 0000000000001111000 # je b (Skip)\nx0x10001011000101111 0000000000001111000 # je c (Skip)\nx0x10001011000111111 0000000000001111000 # je d (Skip)\nx0x10001011001001111 0000000000001111000 # je e (Skip)\nx0x10001011001011111 0000000000001111000 # je bp (Skip)\nx0x10001011001101111 0000000000001111000 # je sp (Skip)\nx0x10001011100001111 0000000000000111000 # jne a(Taken)\nx0x10001011100011111 0000100000000111000 # jne b(Taken)\nx0x10001011100101111 0001000000000111000 # jne c(Taken)\nx0x10001011100111111 0001100000000111000 # jne d(Taken)\nx0x10001011101001111 0010000000000111000 # jne e(Taken)\nx0x10001011101011111 0010100000000111000 # jne bp(Taken)\nx0x10001011101101111 0011000000000111000 # jne sp(Taken)\nx1x10001011100001111 0000000000001111000 # jne a(Skip)\nx1x10001011100011111 0000000000001111000 # jne b(Skip)\nx1x10001011100101111 0000000000001111000 # jne c(Skip)\nx1x10001011100111111 0000000000001111000 # jne d(Skip)\nx1x10001011101001111 0000000000001111000 # jne e(Skip)\nx1x10001011101011111 0000000000001111000 # jne bp(Skip)\nx1x10001011101101111 0000000000001111000 # jne sp(Skip)\nx0010001100000001111 0000000000000111000 # ja a (Taken)\nx0010001100000011111 0000100000000111000 # ja b (Taken)\nx0010001100000101111 0001000000000111000 # ja c (Taken)\nx0010001100000111111 0001100000000111000 # ja d (Taken)\nx0010001100001001111 0010000000000111000 # ja e (Taken)\nx0010001100001011111 0010100000000111000 # ja bp (Taken)\nx0010001100001101111 0011000000000111000 # ja sp (Taken)\nxxx10001100000001111 0000000000001111000 # ja a (Skip)\nxxx10001100000011111 0000000000001111000 # ja b (Skip)\nxxx10001100000101111 0000000000001111000 # ja c (Skip)\nxxx10001100000111111 0000000000001111000 # ja d (Skip)\nxxx10001100001001111 0000000000001111000 # ja e (Skip)\nxxx10001100001011111 0000000000001111000 # ja bp (Skip)\nxxx10001100001101111 0000000000001111000 # ja sp (Skip)\nx0010001100100001111 0000000000000111000 # jae a (Taken)\nx0010001100100011111 0000100000000111000 # jae b (Taken)\nx0010001100100101111 0001000000000111000 # jae c (Taken)\nx0010001100100111111 0001100000000111000 # jae d (Taken)\nx0010001100101001111 0010000000000111000 # jae e (Taken)\nx0010001100101011111 0010100000000111000 # jae bp (Taken)\nx0010001100101101111 0011000000000111000 # jae sp (Taken)\nx1010001100100001111 0000000000000111000 # jae a (Taken)\nx1010001100100011111 0000100000000111000 # jae b (Taken)\nx1010001100100101111 0001000000000111000 # jae c (Taken)\nx1010001100100111111 0001100000000111000 # jae d (Taken)\nx1010001100101001111 0010000000000111000 # jae e (Taken)\nx1010001100101011111 0010100000000111000 # jae bp (Taken)\nx1010001100101101111 0011000000000111000 # jae sp (Taken)\nxxx10001100100001111 0000000000001111000 # jae a (Skip)\nxxx10001100100011111 0000000000001111000 # jae b (Skip)\nxxx10001100100101111 0000000000001111000 # jae c (Skip)\nxxx10001100100111111 0000000000001111000 # jae d (Skip)\nxxx10001100101001111 0000000000001111000 # jae e (Skip)\nxxx10001100101011111 0000000000001111000 # jae bp (Skip)\nxxx10001100101101111 0000000000001111000 # jae sp (Skip)\nx0110001101000001111 0000000000000111000 # jl a (Taken)\nx0110001101000011111 0000100000000111000 # jl b (Taken)\nx0110001101000101111 0001000000000111000 # jl c (Taken)\nx0110001101000111111 0001100000000111000 # jl d (Taken)\nx0110001101001001111 0010000000000111000 # jl e (Taken)\nx0110001101001011111 0010100000000111000 # jl bp (Taken)\nx0110001101001101111 0011000000000111000 # jl sp (Taken)\nxxx10001101000001111 0000000000001111000 # jl a (Skip)\nxxx10001101000011111 0000000000001111000 # jl b (Skip)\nxxx10001101000101111 0000000000001111000 # jl c (Skip)\nxxx10001101000111111 0000000000001111000 # jl d (Skip)\nxxx10001101001001111 0000000000001111000 # jl e (Skip)\nxxx10001101001011111 0000000000001111000 # jl bp (Skip)\nxxx10001101001101111 0000000000001111000 # jl sp (Skip)\nx0110001101100001111 0000000000000111000 # jle a (Taken)\nx0110001101100011111 0000100000000111000 # jle b (Taken)\nx0110001101100101111 0001000000000111000 # jle c (Taken)\nx0110001101100111111 0001100000000111000 # jle d (Taken)\nx0110001101101001111 0010000000000111000 # jle e (Taken)\nx0110001101101011111 0010100000000111000 # jle bp (Taken)\nx0110001101101101111 0011000000000111000 # jle sp (Taken)\nx1010001101100001111 0000000000000111000 # jle a (Taken)\nx1010001101100011111 0000100000000111000 # jle b (Taken)\nx1010001101100101111 0001000000000111000 # jle c (Taken)\nx1010001101100111111 0001100000000111000 # jle d (Taken)\nx1010001101101001111 0010000000000111000 # jle e (Taken)\nx1010001101101011111 0010100000000111000 # jle bp (Taken)\nx1010001101101101111 0011000000000111000 # jle sp (Taken)\nxxx10001101100001111 0000000000001111000 # jle a (Skip)\nxxx10001101100011111 0000000000001111000 # jle b (Skip)\nxxx10001101100101111 0000000000001111000 # jle c (Skip)\nxxx10001101100111111 0000000000001111000 # jle d (Skip)\nxxx10001101101001111 0000000000001111000 # jle e (Skip)\nxxx10001101101011111 0000000000001111000 # jle bp (Skip)\nxxx10001101101101111 0000000000001111000 # jle sp (Skip)")) Instruction_Decoder (
    .in({and_6_out, Instruction_Register_p5}),
    .out({Instruction_Decoder_out[18], Instruction_Decoder_out_2, Instruction_Decoder_out[13], Instruction_Register_p6, Instruction_Decoder_out[9:0]}));
  LED Instruction_Execute (.in(and_6_out[16]));
  D_Flip_Flop d_ff_2 (
    .D(instruction_control_1_ie), .clk(and_2_out), .Q(d_ff_2_q), .reset(button_1_out));  // open: Qn, preset
  not not_9 (not_9_out, Instruction_Decoder_out[18]);
  Adder #(.width(16)) adder_2 (
    .a(demultiplexer_3_out0), .b(demultiplexer_4_out0), .out(adder_2_out), .cin(1'b0), .cout(adder_2_cout));
  Subtractor #(.width(16)) subtractor_1 (
    .a(demultiplexer_3_out1), .b(demultiplexer_4_out1), .out(subtractor_1_out), .bin(1'b0),
    .bout(subtractor_1_bout[0]));
  Multiplier #(.width(16)) multiplier_1 (
    .a(demultiplexer_3_out2), .b(demultiplexer_4_out2), .out(multiplier_1_out), .cin({16{1'b0}}),
    .cout(multiplier_1_cout));
  assign and_7_out = demultiplexer_3_out3 & demultiplexer_4_out3;  // AND_Gate and_7, 16 bits wide
  assign or_1_out = demultiplexer_3_out4 | demultiplexer_4_out4;  // OR_Gate or_1, 16 bits wide
  assign not_10_out = ~demultiplexer_3_out5;  // NOT_Gate not_10, 16 bits wide
  assign xor_1_out = demultiplexer_3_out6 ^ demultiplexer_4_out6;  // XOR_Gate xor_1, 16 bits wide
  LedBar #(.matrixcols(16)) LedBar_2 (
    .led0(multiplexer_22_out[15]), .led1(multiplexer_22_out[14]), .led2(multiplexer_22_out[13]),
    .led3(multiplexer_22_out[12]), .led4(multiplexer_22_out[11]), .led5(multiplexer_22_out[10]),
    .led6(multiplexer_22_out[9]), .led7(multiplexer_22_out[8]), .led8(multiplexer_22_out[7]),
    .led9(multiplexer_22_out[6]), .led10(multiplexer_22_out[5]), .led11(multiplexer_22_out[4]),
    .led12(multiplexer_22_out[3]), .led13(multiplexer_22_out[2]), .led14(multiplexer_22_out[1]),
    .led15(multiplexer_22_out[0]));
  D_Flip_Flop d_ff_3 (.D(and_6_out[16]), .clk(and_1_out), .Q(d_ff_3_q), .reset(RESET_out));  // open: Qn, preset
  Multiplexer #(.select(3), .width(16)) multiplexer_22 (
    .in0(adder_2_out), .in1(subtractor_1_out), .in2(multiplier_1_out), .in3(and_7_out), .in4(or_1_out),
    .in5(not_10_out), .in6(xor_1_out), .in7(right_shifter_1_output_bus_1), .out(multiplexer_22_out),
    .sel(Instruction_Decoder_out[9:7]));
  right_shifter right_shifter_1 (
    .Input_bus_1(demultiplexer_4_out7), .Input_bus_2(demultiplexer_3_out7),
    .carry_out(right_shifter_1_carry_out), .Output_bus_1(right_shifter_1_output_bus_1));
  Register #(.width(16)) register_2 (
    .D({{13{1'b0}}, alu_1_carry_flag}), .en(1'b1), .clk(d_ff_2_q), .Q(register_2_q), .clr(button_1_out));
  or or_2 (subtractor_1_bout[2], adder_2_cout, multiplier_1_cout[7], multiplier_1_cout[0], multiplier_1_cout[1], multiplier_1_cout[2], multiplier_1_cout[3], multiplier_1_cout[4], multiplier_1_cout[5], multiplier_1_cout[6], multiplier_1_cout[8], multiplier_1_cout[9], multiplier_1_cout[10], multiplier_1_cout[11], multiplier_1_cout[12], multiplier_1_cout[13], multiplier_1_cout[14], multiplier_1_cout[15], right_shifter_1_carry_out);
  not not_11 (not_11_out, multiplexer_22_out[0]);
  not not_12 (not_12_out, multiplexer_22_out[1]);
  not not_13 (not_13_out, multiplexer_22_out[2]);
  not not_14 (not_14_out, multiplexer_22_out[3]);
  not not_15 (not_15_out, multiplexer_22_out[4]);
  not not_16 (not_16_out, multiplexer_22_out[5]);
  not not_17 (not_17_out, multiplexer_22_out[6]);
  not not_18 (not_18_out, multiplexer_22_out[7]);
  not not_19 (not_19_out, multiplexer_22_out[8]);
  not not_20 (not_20_out, multiplexer_22_out[9]);
  not not_21 (not_21_out, multiplexer_22_out[10]);
  not not_22 (not_22_out, multiplexer_22_out[11]);
  not not_23 (not_23_out, multiplexer_22_out[12]);
  not not_24 (not_24_out, multiplexer_22_out[13]);
  not not_25 (not_25_out, multiplexer_22_out[14]);
  not not_26 (not_26_out, multiplexer_22_out[15]);
  and and_8 (subtractor_1_bout[1], not_18_out, not_11_out, not_12_out, not_13_out, not_14_out, not_15_out, not_16_out, not_17_out, not_19_out, not_20_out, not_21_out, not_22_out, not_23_out, not_24_out, not_25_out, not_26_out);
  Register #(.width(16)) FLAGS (
    .D({{13{1'b0}}, subtractor_1_bout}), .en(1'b1), .clk(d_ff_3_q), .Q({FLAGS_q, and_6_out[19:17]}),
    .clr(RESET_out));

  // Notes on the sheet:
  //   REGISTERS
endmodule
module right_shifter (
  input  [15:0] Input_bus_1,
  input  [15:0] Input_bus_2,
  output carry_out,
  output [15:0] Output_bus_1
);

  wire and_1_out, and_2_out, and_3_out, and_4_out, and_5_out, and_6_out, and_7_out, and_8_out, and_9_out,
       and_10_out, and_11_out, and_12_out, and_13_out, and_14_out, and_15_out, or_1_out, or_2_out;
  wire [14:0] PLA_1_out;
  wire [15:0] multiplexer_1_out, multiplexer_17_out, multiplexer_33_out, multiplexer_49_out,
       multiplexer_65_out, multiplexer_81_out, multiplexer_97_out, multiplexer_113_out, multiplexer_129_out,
       multiplexer_145_out, multiplexer_161_out, multiplexer_177_out, multiplexer_193_out,
       multiplexer_225_out;

  PLA #(.in_width(16), .out_width(15), .\table ("0000000000000001 000000000000001 # 1\n0000000000000010 000000000000011 # 2\n0000000000000011 000000000000111 # 3\n0000000000000100 000000000001111 # 4\n0000000000000101 000000000011111 # 5\n0000000000000110 000000000111111 # 6\n0000000000000111 000000001111111 # 7\n0000000000001000 000000011111111 # 8\n0000000000001001 000000111111111 # 9\n0000000000001010 000001111111111 # 10\n0000000000001011 000011111111111 # 11\n0000000000001100 000111111111111 # 12\n0000000000001101 001111111111111 # 13\n0000000000001110 011111111111111 # 14\n0000000000001111 111111111111111 # 15")) PLA_1 (
    .in(Input_bus_1), .out(PLA_1_out));
  and and_1 (and_1_out, Input_bus_2[0], PLA_1_out[0]);
  Multiplexer multiplexer_1 (
    .in0(Input_bus_2[0]), .in1(Input_bus_2[1]), .out(multiplexer_1_out[0]), .sel(PLA_1_out[0]));
  Multiplexer multiplexer_2 (
    .in0(Input_bus_2[1]), .in1(Input_bus_2[2]), .out(multiplexer_1_out[1]), .sel(PLA_1_out[0]));
  Multiplexer multiplexer_3 (
    .in0(Input_bus_2[2]), .in1(Input_bus_2[3]), .out(multiplexer_1_out[2]), .sel(PLA_1_out[0]));
  Multiplexer multiplexer_4 (
    .in0(Input_bus_2[3]), .in1(Input_bus_2[4]), .out(multiplexer_1_out[3]), .sel(PLA_1_out[0]));
  Multiplexer multiplexer_5 (
    .in0(Input_bus_2[4]), .in1(Input_bus_2[5]), .out(multiplexer_1_out[4]), .sel(PLA_1_out[0]));
  Multiplexer multiplexer_6 (
    .in0(Input_bus_2[5]), .in1(Input_bus_2[6]), .out(multiplexer_1_out[5]), .sel(PLA_1_out[0]));
  Multiplexer multiplexer_7 (
    .in0(Input_bus_2[6]), .in1(Input_bus_2[7]), .out(multiplexer_1_out[6]), .sel(PLA_1_out[0]));
  Multiplexer multiplexer_8 (
    .in0(Input_bus_2[7]), .in1(Input_bus_2[8]), .out(multiplexer_1_out[7]), .sel(PLA_1_out[0]));
  Multiplexer multiplexer_9 (
    .in0(Input_bus_2[8]), .in1(Input_bus_2[9]), .out(multiplexer_1_out[8]), .sel(PLA_1_out[0]));
  Multiplexer multiplexer_10 (
    .in0(Input_bus_2[9]), .in1(Input_bus_2[10]), .out(multiplexer_1_out[9]), .sel(PLA_1_out[0]));
  Multiplexer multiplexer_11 (
    .in0(Input_bus_2[10]), .in1(Input_bus_2[11]), .out(multiplexer_1_out[10]), .sel(PLA_1_out[0]));
  Multiplexer multiplexer_12 (
    .in0(Input_bus_2[11]), .in1(Input_bus_2[12]), .out(multiplexer_1_out[11]), .sel(PLA_1_out[0]));
  Multiplexer multiplexer_13 (
    .in0(Input_bus_2[12]), .in1(Input_bus_2[13]), .out(multiplexer_1_out[12]), .sel(PLA_1_out[0]));
  Multiplexer multiplexer_14 (
    .in0(Input_bus_2[13]), .in1(Input_bus_2[14]), .out(multiplexer_1_out[13]), .sel(PLA_1_out[0]));
  Multiplexer multiplexer_15 (
    .in0(Input_bus_2[14]), .in1(Input_bus_2[15]), .out(multiplexer_1_out[14]), .sel(PLA_1_out[0]));
  Multiplexer multiplexer_16 (.in0(Input_bus_2[15]), .in1(1'b0), .out(multiplexer_1_out[15]), .sel(PLA_1_out[0]));
  and and_2 (and_2_out, multiplexer_225_out[0], PLA_1_out[8]);
  Multiplexer multiplexer_17 (
    .in0(multiplexer_225_out[0]), .in1(multiplexer_225_out[1]), .out(multiplexer_17_out[0]),
    .sel(PLA_1_out[8]));
  Multiplexer multiplexer_18 (
    .in0(multiplexer_225_out[1]), .in1(multiplexer_225_out[2]), .out(multiplexer_17_out[1]),
    .sel(PLA_1_out[8]));
  Multiplexer multiplexer_19 (
    .in0(multiplexer_225_out[2]), .in1(multiplexer_225_out[3]), .out(multiplexer_17_out[2]),
    .sel(PLA_1_out[8]));
  Multiplexer multiplexer_20 (
    .in0(multiplexer_225_out[3]), .in1(multiplexer_225_out[4]), .out(multiplexer_17_out[3]),
    .sel(PLA_1_out[8]));
  Multiplexer multiplexer_21 (
    .in0(multiplexer_225_out[4]), .in1(multiplexer_225_out[5]), .out(multiplexer_17_out[4]),
    .sel(PLA_1_out[8]));
  Multiplexer multiplexer_22 (
    .in0(multiplexer_225_out[5]), .in1(multiplexer_225_out[6]), .out(multiplexer_17_out[5]),
    .sel(PLA_1_out[8]));
  Multiplexer multiplexer_23 (
    .in0(multiplexer_225_out[6]), .in1(multiplexer_225_out[7]), .out(multiplexer_17_out[6]),
    .sel(PLA_1_out[8]));
  Multiplexer multiplexer_24 (
    .in0(multiplexer_225_out[7]), .in1(multiplexer_225_out[8]), .out(multiplexer_17_out[7]),
    .sel(PLA_1_out[8]));
  Multiplexer multiplexer_25 (
    .in0(multiplexer_225_out[8]), .in1(multiplexer_225_out[9]), .out(multiplexer_17_out[8]),
    .sel(PLA_1_out[8]));
  Multiplexer multiplexer_26 (
    .in0(multiplexer_225_out[9]), .in1(multiplexer_225_out[10]), .out(multiplexer_17_out[9]),
    .sel(PLA_1_out[8]));
  Multiplexer multiplexer_27 (
    .in0(multiplexer_225_out[10]), .in1(multiplexer_225_out[11]), .out(multiplexer_17_out[10]),
    .sel(PLA_1_out[8]));
  Multiplexer multiplexer_28 (
    .in0(multiplexer_225_out[11]), .in1(multiplexer_225_out[12]), .out(multiplexer_17_out[11]),
    .sel(PLA_1_out[8]));
  Multiplexer multiplexer_29 (
    .in0(multiplexer_225_out[12]), .in1(multiplexer_225_out[13]), .out(multiplexer_17_out[12]),
    .sel(PLA_1_out[8]));
  Multiplexer multiplexer_30 (
    .in0(multiplexer_225_out[13]), .in1(multiplexer_225_out[14]), .out(multiplexer_17_out[13]),
    .sel(PLA_1_out[8]));
  Multiplexer multiplexer_31 (
    .in0(multiplexer_225_out[14]), .in1(multiplexer_225_out[15]), .out(multiplexer_17_out[14]),
    .sel(PLA_1_out[8]));
  Multiplexer multiplexer_32 (
    .in0(multiplexer_225_out[15]), .in1(1'b0), .out(multiplexer_17_out[15]), .sel(PLA_1_out[8]));
  and and_3 (and_3_out, multiplexer_1_out[0], PLA_1_out[1]);
  and and_4 (and_4_out, multiplexer_17_out[0], PLA_1_out[9]);
  Multiplexer multiplexer_33 (
    .in0(multiplexer_1_out[0]), .in1(multiplexer_1_out[1]), .out(multiplexer_33_out[0]), .sel(PLA_1_out[1]));
  Multiplexer multiplexer_34 (
    .in0(multiplexer_1_out[1]), .in1(multiplexer_1_out[2]), .out(multiplexer_33_out[1]), .sel(PLA_1_out[1]));
  Multiplexer multiplexer_35 (
    .in0(multiplexer_1_out[2]), .in1(multiplexer_1_out[3]), .out(multiplexer_33_out[2]), .sel(PLA_1_out[1]));
  Multiplexer multiplexer_36 (
    .in0(multiplexer_1_out[3]), .in1(multiplexer_1_out[4]), .out(multiplexer_33_out[3]), .sel(PLA_1_out[1]));
  Multiplexer multiplexer_37 (
    .in0(multiplexer_1_out[4]), .in1(multiplexer_1_out[5]), .out(multiplexer_33_out[4]), .sel(PLA_1_out[1]));
  Multiplexer multiplexer_38 (
    .in0(multiplexer_1_out[5]), .in1(multiplexer_1_out[6]), .out(multiplexer_33_out[5]), .sel(PLA_1_out[1]));
  Multiplexer multiplexer_39 (
    .in0(multiplexer_1_out[6]), .in1(multiplexer_1_out[7]), .out(multiplexer_33_out[6]), .sel(PLA_1_out[1]));
  Multiplexer multiplexer_40 (
    .in0(multiplexer_1_out[7]), .in1(multiplexer_1_out[8]), .out(multiplexer_33_out[7]), .sel(PLA_1_out[1]));
  Multiplexer multiplexer_41 (
    .in0(multiplexer_1_out[8]), .in1(multiplexer_1_out[9]), .out(multiplexer_33_out[8]), .sel(PLA_1_out[1]));
  Multiplexer multiplexer_42 (
    .in0(multiplexer_1_out[9]), .in1(multiplexer_1_out[10]), .out(multiplexer_33_out[9]), .sel(PLA_1_out[1]));
  Multiplexer multiplexer_43 (
    .in0(multiplexer_1_out[10]), .in1(multiplexer_1_out[11]), .out(multiplexer_33_out[10]), .sel(PLA_1_out[1]));
  Multiplexer multiplexer_44 (
    .in0(multiplexer_1_out[11]), .in1(multiplexer_1_out[12]), .out(multiplexer_33_out[11]), .sel(PLA_1_out[1]));
  Multiplexer multiplexer_45 (
    .in0(multiplexer_1_out[12]), .in1(multiplexer_1_out[13]), .out(multiplexer_33_out[12]), .sel(PLA_1_out[1]));
  Multiplexer multiplexer_46 (
    .in0(multiplexer_1_out[13]), .in1(multiplexer_1_out[14]), .out(multiplexer_33_out[13]), .sel(PLA_1_out[1]));
  Multiplexer multiplexer_47 (
    .in0(multiplexer_1_out[14]), .in1(multiplexer_1_out[15]), .out(multiplexer_33_out[14]), .sel(PLA_1_out[1]));
  Multiplexer multiplexer_48 (
    .in0(multiplexer_1_out[15]), .in1(1'b0), .out(multiplexer_33_out[15]), .sel(PLA_1_out[1]));
  Multiplexer multiplexer_49 (
    .in0(multiplexer_17_out[0]), .in1(multiplexer_17_out[1]), .out(multiplexer_49_out[0]), .sel(PLA_1_out[9]));
  Multiplexer multiplexer_50 (
    .in0(multiplexer_17_out[1]), .in1(multiplexer_17_out[2]), .out(multiplexer_49_out[1]), .sel(PLA_1_out[9]));
  Multiplexer multiplexer_51 (
    .in0(multiplexer_17_out[2]), .in1(multiplexer_17_out[3]), .out(multiplexer_49_out[2]), .sel(PLA_1_out[9]));
  Multiplexer multiplexer_52 (
    .in0(multiplexer_17_out[3]), .in1(multiplexer_17_out[4]), .out(multiplexer_49_out[3]), .sel(PLA_1_out[9]));
  Multiplexer multiplexer_53 (
    .in0(multiplexer_17_out[4]), .in1(multiplexer_17_out[5]), .out(multiplexer_49_out[4]), .sel(PLA_1_out[9]));
  Multiplexer multiplexer_54 (
    .in0(multiplexer_17_out[5]), .in1(multiplexer_17_out[6]), .out(multiplexer_49_out[5]), .sel(PLA_1_out[9]));
  Multiplexer multiplexer_55 (
    .in0(multiplexer_17_out[6]), .in1(multiplexer_17_out[7]), .out(multiplexer_49_out[6]), .sel(PLA_1_out[9]));
  Multiplexer multiplexer_56 (
    .in0(multiplexer_17_out[7]), .in1(multiplexer_17_out[8]), .out(multiplexer_49_out[7]), .sel(PLA_1_out[9]));
  Multiplexer multiplexer_57 (
    .in0(multiplexer_17_out[8]), .in1(multiplexer_17_out[9]), .out(multiplexer_49_out[8]), .sel(PLA_1_out[9]));
  Multiplexer multiplexer_58 (
    .in0(multiplexer_17_out[9]), .in1(multiplexer_17_out[10]), .out(multiplexer_49_out[9]), .sel(PLA_1_out[9]));
  Multiplexer multiplexer_59 (
    .in0(multiplexer_17_out[10]), .in1(multiplexer_17_out[11]), .out(multiplexer_49_out[10]),
    .sel(PLA_1_out[9]));
  Multiplexer multiplexer_60 (
    .in0(multiplexer_17_out[11]), .in1(multiplexer_17_out[12]), .out(multiplexer_49_out[11]),
    .sel(PLA_1_out[9]));
  Multiplexer multiplexer_61 (
    .in0(multiplexer_17_out[12]), .in1(multiplexer_17_out[13]), .out(multiplexer_49_out[12]),
    .sel(PLA_1_out[9]));
  Multiplexer multiplexer_62 (
    .in0(multiplexer_17_out[13]), .in1(multiplexer_17_out[14]), .out(multiplexer_49_out[13]),
    .sel(PLA_1_out[9]));
  Multiplexer multiplexer_63 (
    .in0(multiplexer_17_out[14]), .in1(multiplexer_17_out[15]), .out(multiplexer_49_out[14]),
    .sel(PLA_1_out[9]));
  Multiplexer multiplexer_64 (
    .in0(multiplexer_17_out[15]), .in1(1'b0), .out(multiplexer_49_out[15]), .sel(PLA_1_out[9]));
  and and_5 (and_5_out, multiplexer_33_out[0], PLA_1_out[2]);
  Multiplexer multiplexer_65 (
    .in0(multiplexer_33_out[0]), .in1(multiplexer_33_out[1]), .out(multiplexer_65_out[0]), .sel(PLA_1_out[2]));
  Multiplexer multiplexer_66 (
    .in0(multiplexer_33_out[1]), .in1(multiplexer_33_out[2]), .out(multiplexer_65_out[1]), .sel(PLA_1_out[2]));
  Multiplexer multiplexer_67 (
    .in0(multiplexer_33_out[2]), .in1(multiplexer_33_out[3]), .out(multiplexer_65_out[2]), .sel(PLA_1_out[2]));
  Multiplexer multiplexer_68 (
    .in0(multiplexer_33_out[3]), .in1(multiplexer_33_out[4]), .out(multiplexer_65_out[3]), .sel(PLA_1_out[2]));
  Multiplexer multiplexer_69 (
    .in0(multiplexer_33_out[4]), .in1(multiplexer_33_out[5]), .out(multiplexer_65_out[4]), .sel(PLA_1_out[2]));
  Multiplexer multiplexer_70 (
    .in0(multiplexer_33_out[5]), .in1(multiplexer_33_out[6]), .out(multiplexer_65_out[5]), .sel(PLA_1_out[2]));
  Multiplexer multiplexer_71 (
    .in0(multiplexer_33_out[6]), .in1(multiplexer_33_out[7]), .out(multiplexer_65_out[6]), .sel(PLA_1_out[2]));
  Multiplexer multiplexer_72 (
    .in0(multiplexer_33_out[7]), .in1(multiplexer_33_out[8]), .out(multiplexer_65_out[7]), .sel(PLA_1_out[2]));
  Multiplexer multiplexer_73 (
    .in0(multiplexer_33_out[8]), .in1(multiplexer_33_out[9]), .out(multiplexer_65_out[8]), .sel(PLA_1_out[2]));
  Multiplexer multiplexer_74 (
    .in0(multiplexer_33_out[9]), .in1(multiplexer_33_out[10]), .out(multiplexer_65_out[9]), .sel(PLA_1_out[2]));
  Multiplexer multiplexer_75 (
    .in0(multiplexer_33_out[10]), .in1(multiplexer_33_out[11]), .out(multiplexer_65_out[10]),
    .sel(PLA_1_out[2]));
  Multiplexer multiplexer_76 (
    .in0(multiplexer_33_out[11]), .in1(multiplexer_33_out[12]), .out(multiplexer_65_out[11]),
    .sel(PLA_1_out[2]));
  Multiplexer multiplexer_77 (
    .in0(multiplexer_33_out[12]), .in1(multiplexer_33_out[13]), .out(multiplexer_65_out[12]),
    .sel(PLA_1_out[2]));
  Multiplexer multiplexer_78 (
    .in0(multiplexer_33_out[13]), .in1(multiplexer_33_out[14]), .out(multiplexer_65_out[13]),
    .sel(PLA_1_out[2]));
  Multiplexer multiplexer_79 (
    .in0(multiplexer_33_out[14]), .in1(multiplexer_33_out[15]), .out(multiplexer_65_out[14]),
    .sel(PLA_1_out[2]));
  Multiplexer multiplexer_80 (
    .in0(multiplexer_33_out[15]), .in1(1'b0), .out(multiplexer_65_out[15]), .sel(PLA_1_out[2]));
  and and_6 (and_6_out, multiplexer_49_out[0], PLA_1_out[10]);
  Multiplexer multiplexer_81 (
    .in0(multiplexer_49_out[0]), .in1(multiplexer_49_out[1]), .out(multiplexer_81_out[0]), .sel(PLA_1_out[10]));
  Multiplexer multiplexer_82 (
    .in0(multiplexer_49_out[1]), .in1(multiplexer_49_out[2]), .out(multiplexer_81_out[1]), .sel(PLA_1_out[10]));
  Multiplexer multiplexer_83 (
    .in0(multiplexer_49_out[2]), .in1(multiplexer_49_out[3]), .out(multiplexer_81_out[2]), .sel(PLA_1_out[10]));
  Multiplexer multiplexer_84 (
    .in0(multiplexer_49_out[3]), .in1(multiplexer_49_out[4]), .out(multiplexer_81_out[3]), .sel(PLA_1_out[10]));
  Multiplexer multiplexer_85 (
    .in0(multiplexer_49_out[4]), .in1(multiplexer_49_out[5]), .out(multiplexer_81_out[4]), .sel(PLA_1_out[10]));
  Multiplexer multiplexer_86 (
    .in0(multiplexer_49_out[5]), .in1(multiplexer_49_out[6]), .out(multiplexer_81_out[5]), .sel(PLA_1_out[10]));
  Multiplexer multiplexer_87 (
    .in0(multiplexer_49_out[6]), .in1(multiplexer_49_out[7]), .out(multiplexer_81_out[6]), .sel(PLA_1_out[10]));
  Multiplexer multiplexer_88 (
    .in0(multiplexer_49_out[7]), .in1(multiplexer_49_out[8]), .out(multiplexer_81_out[7]), .sel(PLA_1_out[10]));
  Multiplexer multiplexer_89 (
    .in0(multiplexer_49_out[8]), .in1(multiplexer_49_out[9]), .out(multiplexer_81_out[8]), .sel(PLA_1_out[10]));
  Multiplexer multiplexer_90 (
    .in0(multiplexer_49_out[9]), .in1(multiplexer_49_out[10]), .out(multiplexer_81_out[9]),
    .sel(PLA_1_out[10]));
  Multiplexer multiplexer_91 (
    .in0(multiplexer_49_out[10]), .in1(multiplexer_49_out[11]), .out(multiplexer_81_out[10]),
    .sel(PLA_1_out[10]));
  Multiplexer multiplexer_92 (
    .in0(multiplexer_49_out[11]), .in1(multiplexer_49_out[12]), .out(multiplexer_81_out[11]),
    .sel(PLA_1_out[10]));
  Multiplexer multiplexer_93 (
    .in0(multiplexer_49_out[12]), .in1(multiplexer_49_out[13]), .out(multiplexer_81_out[12]),
    .sel(PLA_1_out[10]));
  Multiplexer multiplexer_94 (
    .in0(multiplexer_49_out[13]), .in1(multiplexer_49_out[14]), .out(multiplexer_81_out[13]),
    .sel(PLA_1_out[10]));
  Multiplexer multiplexer_95 (
    .in0(multiplexer_49_out[14]), .in1(multiplexer_49_out[15]), .out(multiplexer_81_out[14]),
    .sel(PLA_1_out[10]));
  Multiplexer multiplexer_96 (
    .in0(multiplexer_49_out[15]), .in1(1'b0), .out(multiplexer_81_out[15]), .sel(PLA_1_out[10]));
  and and_7 (and_7_out, multiplexer_65_out[0], PLA_1_out[3]);
  Multiplexer multiplexer_97 (
    .in0(multiplexer_65_out[0]), .in1(multiplexer_65_out[1]), .out(multiplexer_97_out[0]), .sel(PLA_1_out[3]));
  Multiplexer multiplexer_98 (
    .in0(multiplexer_65_out[1]), .in1(multiplexer_65_out[2]), .out(multiplexer_97_out[1]), .sel(PLA_1_out[3]));
  Multiplexer multiplexer_99 (
    .in0(multiplexer_65_out[2]), .in1(multiplexer_65_out[3]), .out(multiplexer_97_out[2]), .sel(PLA_1_out[3]));
  Multiplexer multiplexer_100 (
    .in0(multiplexer_65_out[3]), .in1(multiplexer_65_out[4]), .out(multiplexer_97_out[3]), .sel(PLA_1_out[3]));
  Multiplexer multiplexer_101 (
    .in0(multiplexer_65_out[4]), .in1(multiplexer_65_out[5]), .out(multiplexer_97_out[4]), .sel(PLA_1_out[3]));
  Multiplexer multiplexer_102 (
    .in0(multiplexer_65_out[5]), .in1(multiplexer_65_out[6]), .out(multiplexer_97_out[5]), .sel(PLA_1_out[3]));
  Multiplexer multiplexer_103 (
    .in0(multiplexer_65_out[6]), .in1(multiplexer_65_out[7]), .out(multiplexer_97_out[6]), .sel(PLA_1_out[3]));
  Multiplexer multiplexer_104 (
    .in0(multiplexer_65_out[7]), .in1(multiplexer_65_out[8]), .out(multiplexer_97_out[7]), .sel(PLA_1_out[3]));
  Multiplexer multiplexer_105 (
    .in0(multiplexer_65_out[8]), .in1(multiplexer_65_out[9]), .out(multiplexer_97_out[8]), .sel(PLA_1_out[3]));
  Multiplexer multiplexer_106 (
    .in0(multiplexer_65_out[9]), .in1(multiplexer_65_out[10]), .out(multiplexer_97_out[9]), .sel(PLA_1_out[3]));
  Multiplexer multiplexer_107 (
    .in0(multiplexer_65_out[10]), .in1(multiplexer_65_out[11]), .out(multiplexer_97_out[10]),
    .sel(PLA_1_out[3]));
  Multiplexer multiplexer_108 (
    .in0(multiplexer_65_out[11]), .in1(multiplexer_65_out[12]), .out(multiplexer_97_out[11]),
    .sel(PLA_1_out[3]));
  Multiplexer multiplexer_109 (
    .in0(multiplexer_65_out[12]), .in1(multiplexer_65_out[13]), .out(multiplexer_97_out[12]),
    .sel(PLA_1_out[3]));
  Multiplexer multiplexer_110 (
    .in0(multiplexer_65_out[13]), .in1(multiplexer_65_out[14]), .out(multiplexer_97_out[13]),
    .sel(PLA_1_out[3]));
  Multiplexer multiplexer_111 (
    .in0(multiplexer_65_out[14]), .in1(multiplexer_65_out[15]), .out(multiplexer_97_out[14]),
    .sel(PLA_1_out[3]));
  Multiplexer multiplexer_112 (
    .in0(multiplexer_65_out[15]), .in1(1'b0), .out(multiplexer_97_out[15]), .sel(PLA_1_out[3]));
  and and_8 (and_8_out, multiplexer_81_out[0], PLA_1_out[11]);
  Multiplexer multiplexer_113 (
    .in0(multiplexer_81_out[0]), .in1(multiplexer_81_out[1]), .out(multiplexer_113_out[0]),
    .sel(PLA_1_out[11]));
  Multiplexer multiplexer_114 (
    .in0(multiplexer_81_out[1]), .in1(multiplexer_81_out[2]), .out(multiplexer_113_out[1]),
    .sel(PLA_1_out[11]));
  Multiplexer multiplexer_115 (
    .in0(multiplexer_81_out[2]), .in1(multiplexer_81_out[3]), .out(multiplexer_113_out[2]),
    .sel(PLA_1_out[11]));
  Multiplexer multiplexer_116 (
    .in0(multiplexer_81_out[3]), .in1(multiplexer_81_out[4]), .out(multiplexer_113_out[3]),
    .sel(PLA_1_out[11]));
  Multiplexer multiplexer_117 (
    .in0(multiplexer_81_out[4]), .in1(multiplexer_81_out[5]), .out(multiplexer_113_out[4]),
    .sel(PLA_1_out[11]));
  Multiplexer multiplexer_118 (
    .in0(multiplexer_81_out[5]), .in1(multiplexer_81_out[6]), .out(multiplexer_113_out[5]),
    .sel(PLA_1_out[11]));
  Multiplexer multiplexer_119 (
    .in0(multiplexer_81_out[6]), .in1(multiplexer_81_out[7]), .out(multiplexer_113_out[6]),
    .sel(PLA_1_out[11]));
  Multiplexer multiplexer_120 (
    .in0(multiplexer_81_out[7]), .in1(multiplexer_81_out[8]), .out(multiplexer_113_out[7]),
    .sel(PLA_1_out[11]));
  Multiplexer multiplexer_121 (
    .in0(multiplexer_81_out[8]), .in1(multiplexer_81_out[9]), .out(multiplexer_113_out[8]),
    .sel(PLA_1_out[11]));
  Multiplexer multiplexer_122 (
    .in0(multiplexer_81_out[9]), .in1(multiplexer_81_out[10]), .out(multiplexer_113_out[9]),
    .sel(PLA_1_out[11]));
  Multiplexer multiplexer_123 (
    .in0(multiplexer_81_out[10]), .in1(multiplexer_81_out[11]), .out(multiplexer_113_out[10]),
    .sel(PLA_1_out[11]));
  Multiplexer multiplexer_124 (
    .in0(multiplexer_81_out[11]), .in1(multiplexer_81_out[12]), .out(multiplexer_113_out[11]),
    .sel(PLA_1_out[11]));
  Multiplexer multiplexer_125 (
    .in0(multiplexer_81_out[12]), .in1(multiplexer_81_out[13]), .out(multiplexer_113_out[12]),
    .sel(PLA_1_out[11]));
  Multiplexer multiplexer_126 (
    .in0(multiplexer_81_out[13]), .in1(multiplexer_81_out[14]), .out(multiplexer_113_out[13]),
    .sel(PLA_1_out[11]));
  Multiplexer multiplexer_127 (
    .in0(multiplexer_81_out[14]), .in1(multiplexer_81_out[15]), .out(multiplexer_113_out[14]),
    .sel(PLA_1_out[11]));
  Multiplexer multiplexer_128 (
    .in0(multiplexer_81_out[15]), .in1(1'b0), .out(multiplexer_113_out[15]), .sel(PLA_1_out[11]));
  and and_9 (and_9_out, multiplexer_97_out[0], PLA_1_out[4]);
  Multiplexer multiplexer_129 (
    .in0(multiplexer_97_out[0]), .in1(multiplexer_97_out[1]), .out(multiplexer_129_out[0]), .sel(PLA_1_out[4]));
  Multiplexer multiplexer_130 (
    .in0(multiplexer_97_out[1]), .in1(multiplexer_97_out[2]), .out(multiplexer_129_out[1]), .sel(PLA_1_out[4]));
  Multiplexer multiplexer_131 (
    .in0(multiplexer_97_out[2]), .in1(multiplexer_97_out[3]), .out(multiplexer_129_out[2]), .sel(PLA_1_out[4]));
  Multiplexer multiplexer_132 (
    .in0(multiplexer_97_out[3]), .in1(multiplexer_97_out[4]), .out(multiplexer_129_out[3]), .sel(PLA_1_out[4]));
  Multiplexer multiplexer_133 (
    .in0(multiplexer_97_out[4]), .in1(multiplexer_97_out[5]), .out(multiplexer_129_out[4]), .sel(PLA_1_out[4]));
  Multiplexer multiplexer_134 (
    .in0(multiplexer_97_out[5]), .in1(multiplexer_97_out[6]), .out(multiplexer_129_out[5]), .sel(PLA_1_out[4]));
  Multiplexer multiplexer_135 (
    .in0(multiplexer_97_out[6]), .in1(multiplexer_97_out[7]), .out(multiplexer_129_out[6]), .sel(PLA_1_out[4]));
  Multiplexer multiplexer_136 (
    .in0(multiplexer_97_out[7]), .in1(multiplexer_97_out[8]), .out(multiplexer_129_out[7]), .sel(PLA_1_out[4]));
  Multiplexer multiplexer_137 (
    .in0(multiplexer_97_out[8]), .in1(multiplexer_97_out[9]), .out(multiplexer_129_out[8]), .sel(PLA_1_out[4]));
  Multiplexer multiplexer_138 (
    .in0(multiplexer_97_out[9]), .in1(multiplexer_97_out[10]), .out(multiplexer_129_out[9]),
    .sel(PLA_1_out[4]));
  Multiplexer multiplexer_139 (
    .in0(multiplexer_97_out[10]), .in1(multiplexer_97_out[11]), .out(multiplexer_129_out[10]),
    .sel(PLA_1_out[4]));
  Multiplexer multiplexer_140 (
    .in0(multiplexer_97_out[11]), .in1(multiplexer_97_out[12]), .out(multiplexer_129_out[11]),
    .sel(PLA_1_out[4]));
  Multiplexer multiplexer_141 (
    .in0(multiplexer_97_out[12]), .in1(multiplexer_97_out[13]), .out(multiplexer_129_out[12]),
    .sel(PLA_1_out[4]));
  Multiplexer multiplexer_142 (
    .in0(multiplexer_97_out[13]), .in1(multiplexer_97_out[14]), .out(multiplexer_129_out[13]),
    .sel(PLA_1_out[4]));
  Multiplexer multiplexer_143 (
    .in0(multiplexer_97_out[14]), .in1(multiplexer_97_out[15]), .out(multiplexer_129_out[14]),
    .sel(PLA_1_out[4]));
  Multiplexer multiplexer_144 (
    .in0(multiplexer_97_out[15]), .in1(1'b0), .out(multiplexer_129_out[15]), .sel(PLA_1_out[4]));
  and and_10 (and_10_out, multiplexer_113_out[0], PLA_1_out[12]);
  Multiplexer multiplexer_145 (
    .in0(multiplexer_113_out[0]), .in1(multiplexer_113_out[1]), .out(multiplexer_145_out[0]),
    .sel(PLA_1_out[12]));
  Multiplexer multiplexer_146 (
    .in0(multiplexer_113_out[1]), .in1(multiplexer_113_out[2]), .out(multiplexer_145_out[1]),
    .sel(PLA_1_out[12]));
  Multiplexer multiplexer_147 (
    .in0(multiplexer_113_out[2]), .in1(multiplexer_113_out[3]), .out(multiplexer_145_out[2]),
    .sel(PLA_1_out[12]));
  Multiplexer multiplexer_148 (
    .in0(multiplexer_113_out[3]), .in1(multiplexer_113_out[4]), .out(multiplexer_145_out[3]),
    .sel(PLA_1_out[12]));
  Multiplexer multiplexer_149 (
    .in0(multiplexer_113_out[4]), .in1(multiplexer_113_out[5]), .out(multiplexer_145_out[4]),
    .sel(PLA_1_out[12]));
  Multiplexer multiplexer_150 (
    .in0(multiplexer_113_out[5]), .in1(multiplexer_113_out[6]), .out(multiplexer_145_out[5]),
    .sel(PLA_1_out[12]));
  Multiplexer multiplexer_151 (
    .in0(multiplexer_113_out[6]), .in1(multiplexer_113_out[7]), .out(multiplexer_145_out[6]),
    .sel(PLA_1_out[12]));
  Multiplexer multiplexer_152 (
    .in0(multiplexer_113_out[7]), .in1(multiplexer_113_out[8]), .out(multiplexer_145_out[7]),
    .sel(PLA_1_out[12]));
  Multiplexer multiplexer_153 (
    .in0(multiplexer_113_out[8]), .in1(multiplexer_113_out[9]), .out(multiplexer_145_out[8]),
    .sel(PLA_1_out[12]));
  Multiplexer multiplexer_154 (
    .in0(multiplexer_113_out[9]), .in1(multiplexer_113_out[10]), .out(multiplexer_145_out[9]),
    .sel(PLA_1_out[12]));
  Multiplexer multiplexer_155 (
    .in0(multiplexer_113_out[10]), .in1(multiplexer_113_out[11]), .out(multiplexer_145_out[10]),
    .sel(PLA_1_out[12]));
  Multiplexer multiplexer_156 (
    .in0(multiplexer_113_out[11]), .in1(multiplexer_113_out[12]), .out(multiplexer_145_out[11]),
    .sel(PLA_1_out[12]));
  Multiplexer multiplexer_157 (
    .in0(multiplexer_113_out[12]), .in1(multiplexer_113_out[13]), .out(multiplexer_145_out[12]),
    .sel(PLA_1_out[12]));
  Multiplexer multiplexer_158 (
    .in0(multiplexer_113_out[13]), .in1(multiplexer_113_out[14]), .out(multiplexer_145_out[13]),
    .sel(PLA_1_out[12]));
  Multiplexer multiplexer_159 (
    .in0(multiplexer_113_out[14]), .in1(multiplexer_113_out[15]), .out(multiplexer_145_out[14]),
    .sel(PLA_1_out[12]));
  Multiplexer multiplexer_160 (
    .in0(multiplexer_113_out[15]), .in1(1'b0), .out(multiplexer_145_out[15]), .sel(PLA_1_out[12]));
  and and_11 (and_11_out, multiplexer_129_out[0], PLA_1_out[5]);
  Multiplexer multiplexer_161 (
    .in0(multiplexer_129_out[0]), .in1(multiplexer_129_out[1]), .out(multiplexer_161_out[0]),
    .sel(PLA_1_out[5]));
  Multiplexer multiplexer_162 (
    .in0(multiplexer_129_out[1]), .in1(multiplexer_129_out[2]), .out(multiplexer_161_out[1]),
    .sel(PLA_1_out[5]));
  Multiplexer multiplexer_163 (
    .in0(multiplexer_129_out[2]), .in1(multiplexer_129_out[3]), .out(multiplexer_161_out[2]),
    .sel(PLA_1_out[5]));
  Multiplexer multiplexer_164 (
    .in0(multiplexer_129_out[3]), .in1(multiplexer_129_out[4]), .out(multiplexer_161_out[3]),
    .sel(PLA_1_out[5]));
  Multiplexer multiplexer_165 (
    .in0(multiplexer_129_out[4]), .in1(multiplexer_129_out[5]), .out(multiplexer_161_out[4]),
    .sel(PLA_1_out[5]));
  Multiplexer multiplexer_166 (
    .in0(multiplexer_129_out[5]), .in1(multiplexer_129_out[6]), .out(multiplexer_161_out[5]),
    .sel(PLA_1_out[5]));
  Multiplexer multiplexer_167 (
    .in0(multiplexer_129_out[6]), .in1(multiplexer_129_out[7]), .out(multiplexer_161_out[6]),
    .sel(PLA_1_out[5]));
  Multiplexer multiplexer_168 (
    .in0(multiplexer_129_out[7]), .in1(multiplexer_129_out[8]), .out(multiplexer_161_out[7]),
    .sel(PLA_1_out[5]));
  Multiplexer multiplexer_169 (
    .in0(multiplexer_129_out[8]), .in1(multiplexer_129_out[9]), .out(multiplexer_161_out[8]),
    .sel(PLA_1_out[5]));
  Multiplexer multiplexer_170 (
    .in0(multiplexer_129_out[9]), .in1(multiplexer_129_out[10]), .out(multiplexer_161_out[9]),
    .sel(PLA_1_out[5]));
  Multiplexer multiplexer_171 (
    .in0(multiplexer_129_out[10]), .in1(multiplexer_129_out[11]), .out(multiplexer_161_out[10]),
    .sel(PLA_1_out[5]));
  Multiplexer multiplexer_172 (
    .in0(multiplexer_129_out[11]), .in1(multiplexer_129_out[12]), .out(multiplexer_161_out[11]),
    .sel(PLA_1_out[5]));
  Multiplexer multiplexer_173 (
    .in0(multiplexer_129_out[12]), .in1(multiplexer_129_out[13]), .out(multiplexer_161_out[12]),
    .sel(PLA_1_out[5]));
  Multiplexer multiplexer_174 (
    .in0(multiplexer_129_out[13]), .in1(multiplexer_129_out[14]), .out(multiplexer_161_out[13]),
    .sel(PLA_1_out[5]));
  Multiplexer multiplexer_175 (
    .in0(multiplexer_129_out[14]), .in1(multiplexer_129_out[15]), .out(multiplexer_161_out[14]),
    .sel(PLA_1_out[5]));
  Multiplexer multiplexer_176 (
    .in0(multiplexer_129_out[15]), .in1(1'b0), .out(multiplexer_161_out[15]), .sel(PLA_1_out[5]));
  and and_12 (and_12_out, multiplexer_145_out[0], PLA_1_out[13]);
  Multiplexer multiplexer_177 (
    .in0(multiplexer_145_out[0]), .in1(multiplexer_145_out[1]), .out(multiplexer_177_out[0]),
    .sel(PLA_1_out[13]));
  Multiplexer multiplexer_178 (
    .in0(multiplexer_145_out[1]), .in1(multiplexer_145_out[2]), .out(multiplexer_177_out[1]),
    .sel(PLA_1_out[13]));
  Multiplexer multiplexer_179 (
    .in0(multiplexer_145_out[2]), .in1(multiplexer_145_out[3]), .out(multiplexer_177_out[2]),
    .sel(PLA_1_out[13]));
  Multiplexer multiplexer_180 (
    .in0(multiplexer_145_out[3]), .in1(multiplexer_145_out[4]), .out(multiplexer_177_out[3]),
    .sel(PLA_1_out[13]));
  Multiplexer multiplexer_181 (
    .in0(multiplexer_145_out[4]), .in1(multiplexer_145_out[5]), .out(multiplexer_177_out[4]),
    .sel(PLA_1_out[13]));
  Multiplexer multiplexer_182 (
    .in0(multiplexer_145_out[5]), .in1(multiplexer_145_out[6]), .out(multiplexer_177_out[5]),
    .sel(PLA_1_out[13]));
  Multiplexer multiplexer_183 (
    .in0(multiplexer_145_out[6]), .in1(multiplexer_145_out[7]), .out(multiplexer_177_out[6]),
    .sel(PLA_1_out[13]));
  Multiplexer multiplexer_184 (
    .in0(multiplexer_145_out[7]), .in1(multiplexer_145_out[8]), .out(multiplexer_177_out[7]),
    .sel(PLA_1_out[13]));
  Multiplexer multiplexer_185 (
    .in0(multiplexer_145_out[8]), .in1(multiplexer_145_out[9]), .out(multiplexer_177_out[8]),
    .sel(PLA_1_out[13]));
  Multiplexer multiplexer_186 (
    .in0(multiplexer_145_out[9]), .in1(multiplexer_145_out[10]), .out(multiplexer_177_out[9]),
    .sel(PLA_1_out[13]));
  Multiplexer multiplexer_187 (
    .in0(multiplexer_145_out[10]), .in1(multiplexer_145_out[11]), .out(multiplexer_177_out[10]),
    .sel(PLA_1_out[13]));
  Multiplexer multiplexer_188 (
    .in0(multiplexer_145_out[11]), .in1(multiplexer_145_out[12]), .out(multiplexer_177_out[11]),
    .sel(PLA_1_out[13]));
  Multiplexer multiplexer_189 (
    .in0(multiplexer_145_out[12]), .in1(multiplexer_145_out[13]), .out(multiplexer_177_out[12]),
    .sel(PLA_1_out[13]));
  Multiplexer multiplexer_190 (
    .in0(multiplexer_145_out[13]), .in1(multiplexer_145_out[14]), .out(multiplexer_177_out[13]),
    .sel(PLA_1_out[13]));
  Multiplexer multiplexer_191 (
    .in0(multiplexer_145_out[14]), .in1(multiplexer_145_out[15]), .out(multiplexer_177_out[14]),
    .sel(PLA_1_out[13]));
  Multiplexer multiplexer_192 (
    .in0(multiplexer_145_out[15]), .in1(1'b0), .out(multiplexer_177_out[15]), .sel(PLA_1_out[13]));
  and and_13 (and_13_out, multiplexer_161_out[0], PLA_1_out[6]);
  and and_14 (and_14_out, multiplexer_177_out[0], PLA_1_out[14]);
  Multiplexer multiplexer_193 (
    .in0(multiplexer_161_out[0]), .in1(multiplexer_161_out[1]), .out(multiplexer_193_out[0]),
    .sel(PLA_1_out[6]));
  Multiplexer multiplexer_194 (
    .in0(multiplexer_161_out[1]), .in1(multiplexer_161_out[2]), .out(multiplexer_193_out[1]),
    .sel(PLA_1_out[6]));
  Multiplexer multiplexer_195 (
    .in0(multiplexer_161_out[2]), .in1(multiplexer_161_out[3]), .out(multiplexer_193_out[2]),
    .sel(PLA_1_out[6]));
  Multiplexer multiplexer_196 (
    .in0(multiplexer_161_out[3]), .in1(multiplexer_161_out[4]), .out(multiplexer_193_out[3]),
    .sel(PLA_1_out[6]));
  Multiplexer multiplexer_197 (
    .in0(multiplexer_161_out[4]), .in1(multiplexer_161_out[5]), .out(multiplexer_193_out[4]),
    .sel(PLA_1_out[6]));
  Multiplexer multiplexer_198 (
    .in0(multiplexer_161_out[5]), .in1(multiplexer_161_out[6]), .out(multiplexer_193_out[5]),
    .sel(PLA_1_out[6]));
  Multiplexer multiplexer_199 (
    .in0(multiplexer_161_out[6]), .in1(multiplexer_161_out[7]), .out(multiplexer_193_out[6]),
    .sel(PLA_1_out[6]));
  Multiplexer multiplexer_200 (
    .in0(multiplexer_161_out[7]), .in1(multiplexer_161_out[8]), .out(multiplexer_193_out[7]),
    .sel(PLA_1_out[6]));
  Multiplexer multiplexer_201 (
    .in0(multiplexer_161_out[8]), .in1(multiplexer_161_out[9]), .out(multiplexer_193_out[8]),
    .sel(PLA_1_out[6]));
  Multiplexer multiplexer_202 (
    .in0(multiplexer_161_out[9]), .in1(multiplexer_161_out[10]), .out(multiplexer_193_out[9]),
    .sel(PLA_1_out[6]));
  Multiplexer multiplexer_203 (
    .in0(multiplexer_161_out[10]), .in1(multiplexer_161_out[11]), .out(multiplexer_193_out[10]),
    .sel(PLA_1_out[6]));
  Multiplexer multiplexer_204 (
    .in0(multiplexer_161_out[11]), .in1(multiplexer_161_out[12]), .out(multiplexer_193_out[11]),
    .sel(PLA_1_out[6]));
  Multiplexer multiplexer_205 (
    .in0(multiplexer_161_out[12]), .in1(multiplexer_161_out[13]), .out(multiplexer_193_out[12]),
    .sel(PLA_1_out[6]));
  Multiplexer multiplexer_206 (
    .in0(multiplexer_161_out[13]), .in1(multiplexer_161_out[14]), .out(multiplexer_193_out[13]),
    .sel(PLA_1_out[6]));
  Multiplexer multiplexer_207 (
    .in0(multiplexer_161_out[14]), .in1(multiplexer_161_out[15]), .out(multiplexer_193_out[14]),
    .sel(PLA_1_out[6]));
  Multiplexer multiplexer_208 (
    .in0(multiplexer_161_out[15]), .in1(1'b0), .out(multiplexer_193_out[15]), .sel(PLA_1_out[6]));
  Multiplexer multiplexer_209 (
    .in0(multiplexer_177_out[0]), .in1(multiplexer_177_out[1]), .out(Output_bus_1[0]), .sel(PLA_1_out[14]));
  Multiplexer multiplexer_210 (
    .in0(multiplexer_177_out[1]), .in1(multiplexer_177_out[2]), .out(Output_bus_1[1]), .sel(PLA_1_out[14]));
  Multiplexer multiplexer_211 (
    .in0(multiplexer_177_out[2]), .in1(multiplexer_177_out[3]), .out(Output_bus_1[2]), .sel(PLA_1_out[14]));
  Multiplexer multiplexer_212 (
    .in0(multiplexer_177_out[3]), .in1(multiplexer_177_out[4]), .out(Output_bus_1[3]), .sel(PLA_1_out[14]));
  Multiplexer multiplexer_213 (
    .in0(multiplexer_177_out[4]), .in1(multiplexer_177_out[5]), .out(Output_bus_1[4]), .sel(PLA_1_out[14]));
  Multiplexer multiplexer_214 (
    .in0(multiplexer_177_out[5]), .in1(multiplexer_177_out[6]), .out(Output_bus_1[5]), .sel(PLA_1_out[14]));
  Multiplexer multiplexer_215 (
    .in0(multiplexer_177_out[6]), .in1(multiplexer_177_out[7]), .out(Output_bus_1[6]), .sel(PLA_1_out[14]));
  Multiplexer multiplexer_216 (
    .in0(multiplexer_177_out[7]), .in1(multiplexer_177_out[8]), .out(Output_bus_1[7]), .sel(PLA_1_out[14]));
  Multiplexer multiplexer_217 (
    .in0(multiplexer_177_out[8]), .in1(multiplexer_177_out[9]), .out(Output_bus_1[8]), .sel(PLA_1_out[14]));
  Multiplexer multiplexer_218 (
    .in0(multiplexer_177_out[9]), .in1(multiplexer_177_out[10]), .out(Output_bus_1[9]), .sel(PLA_1_out[14]));
  Multiplexer multiplexer_219 (
    .in0(multiplexer_177_out[10]), .in1(multiplexer_177_out[11]), .out(Output_bus_1[10]), .sel(PLA_1_out[14]));
  Multiplexer multiplexer_220 (
    .in0(multiplexer_177_out[11]), .in1(multiplexer_177_out[12]), .out(Output_bus_1[11]), .sel(PLA_1_out[14]));
  Multiplexer multiplexer_221 (
    .in0(multiplexer_177_out[12]), .in1(multiplexer_177_out[13]), .out(Output_bus_1[12]), .sel(PLA_1_out[14]));
  Multiplexer multiplexer_222 (
    .in0(multiplexer_177_out[13]), .in1(multiplexer_177_out[14]), .out(Output_bus_1[13]), .sel(PLA_1_out[14]));
  Multiplexer multiplexer_223 (
    .in0(multiplexer_177_out[14]), .in1(multiplexer_177_out[15]), .out(Output_bus_1[14]), .sel(PLA_1_out[14]));
  Multiplexer multiplexer_224 (.in0(multiplexer_177_out[15]), .in1(1'b0), .out(Output_bus_1[15]), .sel(PLA_1_out[14]));
  or or_1 (or_1_out, and_4_out, and_6_out, and_8_out, and_2_out, and_12_out, and_14_out, and_10_out);
  and and_15 (and_15_out, multiplexer_193_out[0], PLA_1_out[7]);
  Multiplexer multiplexer_225 (
    .in0(multiplexer_193_out[0]), .in1(multiplexer_193_out[1]), .out(multiplexer_225_out[0]),
    .sel(PLA_1_out[7]));
  Multiplexer multiplexer_226 (
    .in0(multiplexer_193_out[1]), .in1(multiplexer_193_out[2]), .out(multiplexer_225_out[1]),
    .sel(PLA_1_out[7]));
  Multiplexer multiplexer_227 (
    .in0(multiplexer_193_out[2]), .in1(multiplexer_193_out[3]), .out(multiplexer_225_out[2]),
    .sel(PLA_1_out[7]));
  Multiplexer multiplexer_228 (
    .in0(multiplexer_193_out[3]), .in1(multiplexer_193_out[4]), .out(multiplexer_225_out[3]),
    .sel(PLA_1_out[7]));
  Multiplexer multiplexer_229 (
    .in0(multiplexer_193_out[4]), .in1(multiplexer_193_out[5]), .out(multiplexer_225_out[4]),
    .sel(PLA_1_out[7]));
  Multiplexer multiplexer_230 (
    .in0(multiplexer_193_out[5]), .in1(multiplexer_193_out[6]), .out(multiplexer_225_out[5]),
    .sel(PLA_1_out[7]));
  Multiplexer multiplexer_231 (
    .in0(multiplexer_193_out[6]), .in1(multiplexer_193_out[7]), .out(multiplexer_225_out[6]),
    .sel(PLA_1_out[7]));
  Multiplexer multiplexer_232 (
    .in0(multiplexer_193_out[7]), .in1(multiplexer_193_out[8]), .out(multiplexer_225_out[7]),
    .sel(PLA_1_out[7]));
  Multiplexer multiplexer_233 (
    .in0(multiplexer_193_out[8]), .in1(multiplexer_193_out[9]), .out(multiplexer_225_out[8]),
    .sel(PLA_1_out[7]));
  Multiplexer multiplexer_234 (
    .in0(multiplexer_193_out[9]), .in1(multiplexer_193_out[10]), .out(multiplexer_225_out[9]),
    .sel(PLA_1_out[7]));
  Multiplexer multiplexer_235 (
    .in0(multiplexer_193_out[10]), .in1(multiplexer_193_out[11]), .out(multiplexer_225_out[10]),
    .sel(PLA_1_out[7]));
  Multiplexer multiplexer_236 (
    .in0(multiplexer_193_out[11]), .in1(multiplexer_193_out[12]), .out(multiplexer_225_out[11]),
    .sel(PLA_1_out[7]));
  Multiplexer multiplexer_237 (
    .in0(multiplexer_193_out[12]), .in1(multiplexer_193_out[13]), .out(multiplexer_225_out[12]),
    .sel(PLA_1_out[7]));
  Multiplexer multiplexer_238 (
    .in0(multiplexer_193_out[13]), .in1(multiplexer_193_out[14]), .out(multiplexer_225_out[13]),
    .sel(PLA_1_out[7]));
  Multiplexer multiplexer_239 (
    .in0(multiplexer_193_out[14]), .in1(multiplexer_193_out[15]), .out(multiplexer_225_out[14]),
    .sel(PLA_1_out[7]));
  Multiplexer multiplexer_240 (
    .in0(multiplexer_193_out[15]), .in1(1'b0), .out(multiplexer_225_out[15]), .sel(PLA_1_out[7]));
  or or_2 (or_2_out, and_1_out, and_3_out, and_5_out, and_7_out, and_11_out, and_13_out, and_15_out, and_9_out);
  or or_3 (carry_out, or_2_out, or_1_out);
endmodule

module Instruction_Control (
  input  [15:0] mem_data_in,
  input  [15:0] mem_addr_in,
  input  CLK,
  input  [15:0] pc_data_in,
  input  pc_write_enable,
  input  carry_flag,
  input  zero_flag,
  input  sign_flag,
  input  RESET,
  output [15:0] mem_data_out,
  output [15:0] operand,
  output [15:0] pc_data_out,
  output [17:0] CPU_Control_BUS,
  output IE
);

  wire and_1_out, and_2_out, and_3_out, d_ff_1_q, multiplexer_1_out, not_1_out, not_2_out, not_3_out,
       not_4_out, not_6_out, not_7_out;
  wire [0:0] Instruction_Decoder_out, not_5_out;
  wire [1:0] counter_1_q;
  wire [15:0] adder_1_out, Instruction_Register_p3, Instruction_Register_p5, multiplexer_2_out,
       multiplexer_3_out, multiplexer_4_out, register_1_q;

  Clock clock_1 ();  // open: out
  Multiplexer multiplexer_1 (.in0(pc_write_enable), .in1(1'b1), .out(multiplexer_1_out), .sel(and_1_out));
  and and_1 (and_1_out, d_ff_1_q, not_1_out);
  not not_1 (not_1_out, not_2_out);
  Counter #(.max('hffff), .width(16)) PC (
    .clr(RESET), .load(multiplexer_1_out), .clk(CLK), .D(multiplexer_3_out), .Q(pc_data_out));  // open: up, count, carry
  Multiplexer #(.width(16)) multiplexer_2 (
    .in0(pc_data_out), .in1(pc_data_in), .out(multiplexer_2_out), .sel(multiplexer_1_out));
  Multiplexer #(.width(16)) multiplexer_3 (
    .in0(multiplexer_2_out), .in1(register_1_q), .out(multiplexer_3_out), .sel(and_1_out));
  LedBar #(.matrixcols(16)) LedBar_4 (
    .led0(pc_data_out[15]), .led1(pc_data_out[14]), .led2(pc_data_out[13]), .led3(pc_data_out[12]),
    .led4(pc_data_out[11]), .led5(pc_data_out[10]), .led6(pc_data_out[9]), .led7(pc_data_out[8]),
    .led8(pc_data_out[7]), .led9(pc_data_out[6]), .led10(pc_data_out[5]), .led11(pc_data_out[4]),
    .led12(pc_data_out[3]), .led13(pc_data_out[2]), .led14(pc_data_out[1]), .led15(pc_data_out[0]));
  Register #(.width(16)) register_1 (.D(pc_data_out), .en(1'b1), .clk(CLK), .Q(register_1_q), .clr(RESET));
  not not_2 (not_2_out, and_2_out);
  not not_3 (not_3_out, CPU_Control_BUS[0]);
  and and_2 (and_2_out, not_3_out, not_4_out);
  not not_4 (not_4_out, CPU_Control_BUS[1]);
  D_Flip_Flop d_ff_1 (.D(not_2_out), .clk(CLK), .Q(d_ff_1_q), .reset(RESET));  // open: Qn, preset
  Adder #(.width(16)) adder_1 (.a(mem_addr_in), .b(operand), .out(adder_1_out), .cin(1'b0));  // open: cout
  Multiplexer #(.select(2), .width(16)) multiplexer_4 (
    .in0(pc_data_out), .in1(adder_1_out), .in2(operand), .out(multiplexer_4_out), .sel(CPU_Control_BUS[1:0]));  // open: in3
  RAM #(.addrWidth(16), .dataWidth(16), .enables("line")) RAM_1 (
    .addr(multiplexer_4_out), .we(Instruction_Decoder_out[0]), .clk(CLK), .din(mem_data_in),
    .dout(mem_data_out));
  // Shift_Register #(.length(2), .width(16)) Instruction_Register: pin names not known; wires that end beside it: RESET, CLK, Instruction_Register_p3, operand, Instruction_Register_p5
  Multiplexer #(.width(16)) multiplexer_5 (
    .in0(mem_data_out), .in1({16{1'b1}}), .out(Instruction_Register_p3), .sel(not_2_out));
  Counter #(.max('h3), .width(2)) counter_1 (
    .clr(RESET), .load(IE), .clk(CLK), .D({1'b0, not_5_out[0]}), .Q(counter_1_q));  // open: up, count, carry
  not not_5 (not_5_out[0], and_3_out);
  and and_3 (and_3_out, CPU_Control_BUS[2], CPU_Control_BUS[3], CPU_Control_BUS[4], not_6_out);
  not not_6 (not_6_out, CPU_Control_BUS[5]);
  not not_7 (not_7_out, counter_1_q[0]);
  and and_4 (IE, not_7_out, counter_1_q[1]);
  LED Instruction_Execute (.in(IE));
  PLA #(.in_width(20), .out_width(19), .\table ("xxx0xxxxxxxxxxxxxxxx 0000000000001111000 # IE=0 (during fetch)\n0xx10000101111111111 0011100000000111000 # jnc opd (Taken)\n1xx10000101111111111 0000000000001111000 # jnc opd (Skip)\n1xx10000110011111111 0011100000000111000 # jc opd (Taken)\n0xx10000110011111111 0000000000001111000 # jc opd (Skip)\nx0x10000110111111111 0011100000000111000 # jnz opd (Taken)\nx1x10000110111111111 0000000000001111000 # jnz opd (Skip)\nx1x10000111011111111 0011100000000111000 # jz opd (Taken)\nx0x10000111011111111 0000000000001111000 # jz opd (Skip)\nxx010000111111111111 0011100000000111000 # jns opd (Taken)\nxx110000111111111111 0000000000001111000 # jns opd (Skip)\nxx110001000011111111 0011100000000111000 # js opd (Taken)\nxx010001000011111111 0000000000001111000 # js opd (Skip)\nxxx10001000111111111 0011100000000111000 # jmp opd\nx1x10001011011111111 0011100000000111000 # je opd (Taken)\nx0x10001011011111111 0000000000001111000 # je opd (Skip)\nx0x10001011111111111 0011100000000111000 # jne opd(Taken)\nx1x10001011111111111 0000000000001111000 # jne opd(Skip)\nx0010001100011111111 0011100000000111000 # ja opd (Taken)\nxxx10001100011111111 0000000000001111000 # ja opd (Skip)\nx0010001100111111111 0011100000000111000 # jae opd (Taken)\nx1010001100111111111 0011100000000111000 # jae opd (Taken)\nxxx10001100111111111 0000000000001111000 # jae opd (Skip)\nx0110001101011111111 0011100000000111000 # jl opd (Taken)\nxxx10001101011111111 0000000000001111000 # jl opd (Skip)\nx0110001101111111111 0011100000000111000 # jle opd (Taken)\nx1010001101111111111 0011100000000111000 # jle opd (Taken)\nxxx10001101111111111 0000000000001111000 # jle opd (Skip)\nxxx10001001111111111 1000000000001111000 # hlt\nxxx10001010011111111 0000000000001111000 # nop\nxxxx1111111111111111 0000000000001111000 # invaild\nxxx10001010111111111 0101000000001010000 # lpc\nxxx10000000000000000 0000010000000000000 # add a, a\nxxx10000000000000001 0000010010000000000 # add a, b\nxxx10000000000000010 0000010100000000000 # add a, c\nxxx10000000000000011 0000010110000000000 # add a, d\nxxx10000000000000100 0000011000000000000 # add a, e\nxxx10000000000000101 0000011010000000000 # add a, bp\nxxx10000000000000110 0000011100000000000 # add a, sp\nxxx10000000000010000 0000110000000001000 # add b, a\nxxx10000000000010001 0000110010000001000 # add b, b\nxxx10000000000010010 0000110100000001000 # add b, c\nxxx10000000000010011 0000110110000001000 # add b, d\nxxx10000000000010100 0000111000000001000 # add b, e\nxxx10000000000010101 0000111010000001000 # add b, bp\nxxx10000000000010110 0000111100000001000 # add b, sp\nxxx10000000000100000 0001010000000010000 # add c, a\nxxx10000000000100001 0001010010000010000 # add c, b\nxxx10000000000100010 0001010100000010000 # add c, c\nxxx10000000000100011 0001010110000010000 # add c, d\nxxx10000000000100100 0001011000000010000 # add c, e\nxxx10000000000100101 0001011010000010000 # add c, bp\nxxx10000000000100110 0001011100000010000 # add c, sp\nxxx10000000000110000 0001110000000011000 # add d, a\nxxx10000000000110001 0001110010000011000 # add d, b\nxxx10000000000110010 0001110100000011000 # add d, c\nxxx10000000000110011 0001110110000011000 # add d, d\nxxx10000000000110100 0001111000000011000 # add d, e\nxxx10000000000110101 0001111010000011000 # add d, bp\nxxx10000000000110110 0001111100000011000 # add d, sp\nxxx10000000001000000 0010010000000100000 # add e, a\nxxx10000000001000001 0010010010000100000 # add e, b\nxxx10000000001000010 0010010100000100000 # add e, c\nxxx10000000001000011 0010010110000100000 # add e, d\nxxx10000000001000100 0010011000000100000 # add e, e\nxxx10000000001000101 0010011010000100000 # add e, bp\nxxx10000000001000110 0010011100000100000 # add e, sp\nxxx10000000001010000 0010110000000101000 # add bp, a\nxxx10000000001010001 0010110010000101000 # add bp, b\nxxx10000000001010010 0010110100000101000 # add bp, c\nxxx10000000001010011 0010110110000101000 # add bp, d\nxxx10000000001010100 0010111000000101000 # add bp, e\nxxx10000000001010101 0010111010000101000 # add bp, bp\nxxx10000000001010110 0010111100000101000 # add bp, sp\nxxx10000000001100000 0011010000000110000 # add sp, a\nxxx10000000001100001 0011010010000110000 # add sp, b\nxxx10000000001100010 0011010100000110000 # add sp, c\nxxx10000000001100011 0011010110000110000 # add sp, d\nxxx10000000001100100 0011011000000110000 # add sp, e\nxxx10000000001100101 0011011010000110000 # add sp, bp\nxxx10000000001100110 0011011100000110000 # add sp, sp\nxxx10000000100000000 0000010000010000000 # sub a, a\nxxx10000000100000001 0000010010010000000 # sub a, b\nxxx10000000100000010 0000010100010000000 # sub a, c\nxxx10000000100000011 0000010110010000000 # sub a, d\nxxx10000000100000100 0000011000010000000 # sub a, e\nxxx10000000100000101 0000011010010000000 # sub a, bp\nxxx10000000100000110 0000011100010000000 # sub a, sp\nxxx10000000100010000 0000110000010001000 # sub b, a\nxxx10000000100010001 0000110010010001000 # sub b, b\nxxx10000000100010010 0000110100010001000 # sub b, c\nxxx10000000100010011 0000110110010001000 # sub b, d\nxxx10000000100010100 0000111000010001000 # sub b, e\nxxx10000000100010101 0000111010010001000 # sub b, bp\nxxx10000000100010110 0000111100010001000 # sub b, sp\nxxx10000000100100000 0001010000010010000 # sub c, a\nxxx10000000100100001 0001010010010010000 # sub c, b\nxxx10000000100100010 0001010100010010000 # sub c, c\nxxx10000000100100011 0001010110010010000 # sub c, d\nxxx10000000100100100 0001011000010010000 # sub c, e\nxxx10000000100100101 0001011010010010000 # sub c, bp\nxxx10000000100100110 0001011100010010000 # sub c, sp\nxxx10000000100110000 0001110000010011000 # sub d, a\nxxx10000000100110001 0001110010010011000 # sub d, b\nxxx10000000100110010 0001110100010011000 # sub d, c\nxxx10000000100110011 0001110110010011000 # sub d, d\nxxx10000000100110100 0001111000010011000 # sub d, e\nxxx10000000100110101 0001111010010011000 # sub d, bp\nxxx10000000100110110 0001111100010011000 # sub d, sp\nxxx10000000101000000 0010010000010100000 # sub e, a\nxxx10000000101000001 0010010010010100000 # sub e, b\nxxx10000000101000010 0010010100010100000 # sub e, c\nxxx10000000101000011 0010010110010100000 # sub e, d\nxxx10000000101000100 0010011000010100000 # sub e, e\nxxx10000000101000101 0010011010010100000 # sub e, bp\nxxx10000000101000110 0010011100010100000 # sub e, sp\nxxx10000000101010000 0010110000010101000 # sub bp, a\nxxx10000000101010001 0010110010010101000 # sub bp, b\nxxx10000000101010010 0010110100010101000 # sub bp, c\nxxx10000000101010011 0010110110010101000 # sub bp, d\nxxx10000000101010100 0010111000010101000 # sub bp, e\nxxx10000000101010101 0010111010010101000 # sub bp, bp\nxxx10000000101010110 0010111100010101000 # sub bp, sp\nxxx10000000101100000 0011010000010110000 # sub sp, a\nxxx10000000101100001 0011010010010110000 # sub sp, b\nxxx10000000101100010 0011010100010110000 # sub sp, c\nxxx10000000101100011 0011010110010110000 # sub sp, d\nxxx10000000101100100 0011011000010110000 # sub sp, e\nxxx10000000101100101 0011011010010110000 # sub sp, bp\nxxx10000000101100110 0011011100010110000 # sub sp, sp\nxxx10000001000000000 0000010000100000000 # mul a, a\nxxx10000001000000001 0000010010100000000 # mul a, b\nxxx10000001000000010 0000010100100000000 # mul a, c\nxxx10000001000000011 0000010110100000000 # mul a, d\nxxx10000001000000100 0000011000100000000 # mul a, e\nxxx10000001000000101 0000011010100000000 # mul a, bp\nxxx10000001000000110 0000011100100000000 # mul a, sp\nxxx10000001000010000 0000110000100001000 # mul b, a\nxxx10000001000010001 0000110010100001000 # mul b, b\nxxx10000001000010010 0000110100100001000 # mul b, c\nxxx10000001000010011 0000110110100001000 # mul b, d\nxxx10000001000010100 0000111000100001000 # mul b, e\nxxx10000001000010101 0000111010100001000 # mul b, bp\nxxx10000001000010110 0000111100100001000 # mul b, sp\nxxx10000001000100000 0001010000100010000 # mul c, a\nxxx10000001000100001 0001010010100010000 # mul c, b\nxxx10000001000100010 0001010100100010000 # mul c, c\nxxx10000001000100011 0001010110100010000 # mul c, d\nxxx10000001000100100 0001011000100010000 # mul c, e\nxxx10000001000100101 0001011010100010000 # mul c, bp\nxxx10000001000100110 0001011100100010000 # mul c, sp\nxxx10000001000110000 0001110000100011000 # mul d, a\nxxx10000001000110001 0001110010100011000 # mul d, b\nxxx10000001000110010 0001110100100011000 # mul d, c\nxxx10000001000110011 0001110110100011000 # mul d, d\nxxx10000001000110100 0001111000100011000 # mul d, e\nxxx10000001000110101 0001111010100011000 # mul d, bp\nxxx10000001000110110 0001111100100011000 # mul d, sp\nxxx10000001001000000 0010010000100100000 # mul e, a\nxxx10000001001000001 0010010010100100000 # mul e, b\nxxx10000001001000010 0010010100100100000 # mul e, c\nxxx10000001001000011 0010010110100100000 # mul e, d\nxxx10000001001000100 0010011000100100000 # mul e, e\nxxx10000001001000101 0010011010100100000 # mul e, bp\nxxx10000001001000110 0010011100100100000 # mul e, sp\nxxx10000001001010000 0010110000100101000 # mul bp, a\nxxx10000001001010001 0010110010100101000 # mul bp, b\nxxx10000001001010010 0010110100100101000 # mul bp, c\nxxx10000001001010011 0010110110100101000 # mul bp, d\nxxx10000001001010100 0010111000100101000 # mul bp, e\nxxx10000001001010101 0010111010100101000 # mul bp, bp\nxxx10000001001010110 0010111100100101000 # mul bp, sp\nxxx10000001001100000 0011010000100110000 # mul sp, a\nxxx10000001001100001 0011010010100110000 # mul sp, b\nxxx10000001001100010 0011010100100110000 # mul sp, c\nxxx10000001001100011 0011010110100110000 # mul sp, d\nxxx10000001001100100 0011011000100110000 # mul sp, e\nxxx10000001001100101 0011011010100110000 # mul sp, bp\nxxx10000001001100110 0011011100100110000 # mul sp, sp\nxxx10000001100000000 0000010000110000000 # and a, a\nxxx10000001100000001 0000010010110000000 # and a, b\nxxx10000001100000010 0000010100110000000 # and a, c\nxxx10000001100000011 0000010110110000000 # and a, d\nxxx10000001100000100 0000011000110000000 # and a, e\nxxx10000001100000101 0000011010110000000 # and a, bp\nxxx10000001100000110 0000011100110000000 # and a, sp\nxxx10000001100010000 0000110000110001000 # and b, a\nxxx10000001100010001 0000110010110001000 # and b, b\nxxx10000001100010010 0000110100110001000 # and b, c\nxxx10000001100010011 0000110110110001000 # and b, d\nxxx10000001100010100 0000111000110001000 # and b, e\nxxx10000001100010101 0000111010110001000 # and b, bp\nxxx10000001100010110 0000111100110001000 # and b, sp\nxxx10000001100100000 0001010000110010000 # and c, a\nxxx10000001100100001 0001010010110010000 # and c, b\nxxx10000001100100010 0001010100110010000 # and c, c\nxxx10000001100100011 0001010110110010000 # and c, d\nxxx10000001100100100 0001011000110010000 # and c, e\nxxx10000001100100101 0001011010110010000 # and c, bp\nxxx10000001100100110 0001011100110010000 # and c, sp\nxxx10000001100110000 0001110000110011000 # and d, a\nxxx10000001100110001 0001110010110011000 # and d, b\nxxx10000001100110010 0001110100110011000 # and d, c\nxxx10000001100110011 0001110110110011000 # and d, d\nxxx10000001100110100 0001111000110011000 # and d, e\nxxx10000001100110101 0001111010110011000 # and d, bp\nxxx10000001100110110 0001111100110011000 # and d, sp\nxxx10000001101000000 0010010000110100000 # and e, a\nxxx10000001101000001 0010010010110100000 # and e, b\nxxx10000001101000010 0010010100110100000 # and e, c\nxxx10000001101000011 0010010110110100000 # and e, d\nxxx10000001101000100 0010011000110100000 # and e, e\nxxx10000001101000101 0010011010110100000 # and e, bp\nxxx10000001101000110 0010011100110100000 # and e, sp\nxxx10000001101010000 0010110000110101000 # and bp, a\nxxx10000001101010001 0010110010110101000 # and bp, b\nxxx10000001101010010 0010110100110101000 # and bp, c\nxxx10000001101010011 0010110110110101000 # and bp, d\nxxx10000001101010100 0010111000110101000 # and bp, e\nxxx10000001101010101 0010111010110101000 # and bp, bp\nxxx10000001101010110 0010111100110101000 # and bp, sp\nxxx10000001101100000 0011010000110110000 # and sp, a\nxxx10000001101100001 0011010010110110000 # and sp, b\nxxx10000001101100010 0011010100110110000 # and sp, c\nxxx10000001101100011 0011010110110110000 # and sp, d\nxxx10000001101100100 0011011000110110000 # and sp, e\nxxx10000001101100101 0011011010110110000 # and sp, bp\nxxx10000001101100110 0011011100110110000 # and sp, sp\nxxx10000010000000000 0000010001000000000 # or a, a\nxxx10000010000000001 0000010011000000000 # or a, b\nxxx10000010000000010 0000010101000000000 # or a, c\nxxx10000010000000011 0000010111000000000 # or a, d\nxxx10000010000000100 0000011001000000000 # or a, e\nxxx10000010000000101 0000011011000000000 # or a, bp\nxxx10000010000000110 0000011101000000000 # or a, sp\nxxx10000010000010000 0000110001000001000 # or b, a\nxxx10000010000010001 0000110011000001000 # or b, b\nxxx10000010000010010 0000110101000001000 # or b, c\nxxx10000010000010011 0000110111000001000 # or b, d\nxxx10000010000010100 0000111001000001000 # or b, e\nxxx10000010000010101 0000111011000001000 # or b, bp\nxxx10000010000010110 0000111101000001000 # or b, sp\nxxx10000010000100000 0001010001000010000 # or c, a\nxxx10000010000100001 0001010011000010000 # or c, b\nxxx10000010000100010 0001010101000010000 # or c, c\nxxx10000010000100011 0001010111000010000 # or c, d\nxxx10000010000100100 0001011001000010000 # or c, e\nxxx10000010000100101 0001011011000010000 # or c, bp\nxxx10000010000100110 0001011101000010000 # or c, sp\nxxx10000010000110000 0001110001000011000 # or d, a\nxxx10000010000110001 0001110011000011000 # or d, b\nxxx10000010000110010 0001110101000011000 # or d, c\nxxx10000010000110011 0001110111000011000 # or d, d\nxxx10000010000110100 0001111001000011000 # or d, e\nxxx10000010000110101 0001111011000011000 # or d, bp\nxxx10000010000110110 0001111101000011000 # or d, sp\nxxx10000010001000000 0010010001000100000 # or e, a\nxxx10000010001000001 0010010011000100000 # or e, b\nxxx10000010001000010 0010010101000100000 # or e, c\nxxx10000010001000011 0010010111000100000 # or e, d\nxxx10000010001000100 0010011001000100000 # or e, e\nxxx10000010001000101 0010011011000100000 # or e, bp\nxxx10000010001000110 0010011101000100000 # or e, sp\nxxx10000010001010000 0010110001000101000 # or bp, a\nxxx10000010001010001 0010110011000101000 # or bp, b\nxxx10000010001010010 0010110101000101000 # or bp, c\nxxx10000010001010011 0010110111000101000 # or bp, d\nxxx10000010001010100 0010111001000101000 # or bp, e\nxxx10000010001010101 0010111011000101000 # or bp, bp\nxxx10000010001010110 0010111101000101000 # or bp, sp\nxxx10000010001100000 0011010001000110000 # or sp, a\nxxx10000010001100001 0011010011000110000 # or sp, b\nxxx10000010001100010 0011010101000110000 # or sp, c\nxxx10000010001100011 0011010111000110000 # or sp, d\nxxx10000010001100100 0011011001000110000 # or sp, e\nxxx10000010001100101 0011011011000110000 # or sp, bp\nxxx10000010001100110 0011011101000110000 # or sp, sp\nxxx10000011000000000 0000010001100000000 # xor a, a\nxxx10000011000000001 0000010011100000000 # xor a, b\nxxx10000011000000010 0000010101100000000 # xor a, c\nxxx10000011000000011 0000010111100000000 # xor a, d\nxxx10000011000000100 0000011001100000000 # xor a, e\nxxx10000011000000101 0000011011100000000 # xor a, bp\nxxx10000011000000110 0000011101100000000 # xor a, sp\nxxx10000011000010000 0000110001100001000 # xor b, a\nxxx10000011000010001 0000110011100001000 # xor b, b\nxxx10000011000010010 0000110101100001000 # xor b, c\nxxx10000011000010011 0000110111100001000 # xor b, d\nxxx10000011000010100 0000111001100001000 # xor b, e\nxxx10000011000010101 0000111011100001000 # xor b, bp\nxxx10000011000010110 0000111101100001000 # xor b, sp\nxxx10000011000100000 0001010001100010000 # xor c, a\nxxx10000011000100001 0001010011100010000 # xor c, b\nxxx10000011000100010 0001010101100010000 # xor c, c\nxxx10000011000100011 0001010111100010000 # xor c, d\nxxx10000011000100100 0001011001100010000 # xor c, e\nxxx10000011000100101 0001011011100010000 # xor c, bp\nxxx10000011000100110 0001011101100010000 # xor c, sp\nxxx10000011000110000 0001110001100011000 # xor d, a\nxxx10000011000110001 0001110011100011000 # xor d, b\nxxx10000011000110010 0001110101100011000 # xor d, c\nxxx10000011000110011 0001110111100011000 # xor d, d\nxxx10000011000110100 0001111001100011000 # xor d, e\nxxx10000011000110101 0001111011100011000 # xor d, bp\nxxx10000011000110110 0001111101100011000 # xor d, sp\nxxx10000011001000000 0010010001100100000 # xor e, a\nxxx10000011001000001 0010010011100100000 # xor e, b\nxxx10000011001000010 0010010101100100000 # xor e, c\nxxx10000011001000011 0010010111100100000 # xor e, d\nxxx10000011001000100 0010011001100100000 # xor e, e\nxxx10000011001000101 0010011011100100000 # xor e, bp\nxxx10000011001000110 0010011101100100000 # xor e, sp\nxxx10000011001010000 0010110001100101000 # xor bp, a\nxxx10000011001010001 0010110011100101000 # xor bp, b\nxxx10000011001010010 0010110101100101000 # xor bp, c\nxxx10000011001010011 0010110111100101000 # xor bp, d\nxxx10000011001010100 0010111001100101000 # xor bp, e\nxxx10000011001010101 0010111011100101000 # xor bp, bp\nxxx10000011001010110 0010111101100101000 # xor bp, sp\nxxx10000011001100000 0011010001100110000 # xor sp, a\nxxx10000011001100001 0011010011100110000 # xor sp, b\nxxx10000011001100010 0011010101100110000 # xor sp, c\nxxx10000011001100011 0011010111100110000 # xor sp, d\nxxx10000011001100100 0011011001100110000 # xor sp, e\nxxx10000011001100101 0011011011100110000 # xor sp, bp\nxxx10000011001100110 0011011101100110000 # xor sp, sp\nxxx10000011100000000 0000010001110000000 # shr a, a\nxxx10000011100000001 0000010011110000000 # shr a, b\nxxx10000011100000010 0000010101110000000 # shr a, c\nxxx10000011100000011 0000010111110000000 # shr a, d\nxxx10000011100000100 0000011001110000000 # shr a, e\nxxx10000011100000101 0000011011110000000 # shr a, bp\nxxx10000011100000110 0000011101110000000 # shr a, sp\nxxx10000011100010000 0000110001110001000 # shr b, a\nxxx10000011100010001 0000110011110001000 # shr b, b\nxxx10000011100010010 0000110101110001000 # shr b, c\nxxx10000011100010011 0000110111110001000 # shr b, d\nxxx10000011100010100 0000111001110001000 # shr b, e\nxxx10000011100010101 0000111011110001000 # shr b, bp\nxxx10000011100010110 0000111101110001000 # shr b, sp\nxxx10000011100100000 0001010001110010000 # shr c, a\nxxx10000011100100001 0001010011110010000 # shr c, b\nxxx10000011100100010 0001010101110010000 # shr c, c\nxxx10000011100100011 0001010111110010000 # shr c, d\nxxx10000011100100100 0001011001110010000 # shr c, e\nxxx10000011100100101 0001011011110010000 # shr c, bp\nxxx10000011100100110 0001011101110010000 # shr c, sp\nxxx10000011100110000 0001110001110011000 # shr d, a\nxxx10000011100110001 0001110011110011000 # shr d, b\nxxx10000011100110010 0001110101110011000 # shr d, c\nxxx10000011100110011 0001110111110011000 # shr d, d\nxxx10000011100110100 0001111001110011000 # shr d, e\nxxx10000011100110101 0001111011110011000 # shr d, bp\nxxx10000011100110110 0001111101110011000 # shr d, sp\nxxx10000011101000000 0010010001110100000 # shr e, a\nxxx10000011101000001 0010010011110100000 # shr e, b\nxxx10000011101000010 0010010101110100000 # shr e, c\nxxx10000011101000011 0010010111110100000 # shr e, d\nxxx10000011101000100 0010011001110100000 # shr e, e\nxxx10000011101000101 0010011011110100000 # shr e, bp\nxxx10000011101000110 0010011101110100000 # shr e, sp\nxxx10000011101010000 0010110001110101000 # shr bp, a\nxxx10000011101010001 0010110011110101000 # shr bp, b\nxxx10000011101010010 0010110101110101000 # shr bp, c\nxxx10000011101010011 0010110111110101000 # shr bp, d\nxxx10000011101010100 0010111001110101000 # shr bp, e\nxxx10000011101010101 0010111011110101000 # shr bp, bp\nxxx10000011101010110 0010111101110101000 # shr bp, sp\nxxx10000011101100000 0011010001110110000 # shr sp, a\nxxx10000011101100001 0011010011110110000 # shr sp, b\nxxx10000011101100010 0011010101110110000 # shr sp, c\nxxx10000011101100011 0011010111110110000 # shr sp, d\nxxx10000011101100100 0011011001110110000 # shr sp, e\nxxx10000011101100101 0011011011110110000 # shr sp, bp\nxxx10000011101100110 0011011101110110000 # shr sp, sp\nxxx10000000000001111 0000011110000000000 # add a, opd\nxxx10000000000011111 0000111110000001000 # add b, opd\nxxx10000000000101111 0001011110000010000 # add c, opd\nxxx10000000000111111 0001111110000011000 # add d, opd\nxxx10000000001001111 0010011110000100000 # add e, opd\nxxx10000000001011111 0010111110000101000 # add bp, opd\nxxx10000000001101111 0011011110000110000 # add sp, opd\nxxx10000000100001111 0000011110010000000 # sub a, opd\nxxx10000000100011111 0000111110010001000 # sub b, opd\nxxx10000000100101111 0001011110010010000 # sub c, opd\nxxx10000000100111111 0001111110010011000 # sub d, opd\nxxx10000000101001111 0010011110010100000 # sub e, opd\nxxx10000000101011111 0010111110010101000 # sub bp, opd\nxxx10000000101101111 0011011110010110000 # sub sp, opd\nxxx10000001000001111 0000011110100000000 # mul a, opd\nxxx10000001000011111 0000111110100001000 # mul b, opd\nxxx10000001000101111 0001011110100010000 # mul c, opd\nxxx10000001000111111 0001111110100011000 # mul d, opd\nxxx10000001001001111 0010011110100100000 # mul e, opd\nxxx10000001001011111 0010111110100101000 # mul bp, opd\nxxx10000001001101111 0011011110100110000 # mul sp, opd\nxxx10000001100001111 0000011110110000000 # and a, opd\nxxx10000001100011111 0000111110110001000 # and b, opd\nxxx10000001100101111 0001011110110010000 # and c, opd\nxxx10000001100111111 0001111110110011000 # and d, opd\nxxx10000001101001111 0010011110110100000 # and e, opd\nxxx10000001101011111 0010111110110101000 # and bp, opd\nxxx10000001101101111 0011011110110110000 # and sp, opd\nxxx10000010000001111 0000011111000000000 # or a, opd\nxxx10000010000011111 0000111111000001000 # or b, opd\nxxx10000010000101111 0001011111000010000 # or c, opd\nxxx10000010000111111 0001111111000011000 # or d, opd\nxxx10000010001001111 0010011111000100000 # or e, opd\nxxx10000010001011111 0010111111000101000 # or bp, opd\nxxx10000010001101111 0011011111000110000 # or sp, opd\nxxx10000011000001111 0000011111100000000 # xor a, opd\nxxx10000011000011111 0000111111100001000 # xor b, opd\nxxx10000011000101111 0001011111100010000 # xor c, opd\nxxx10000011000111111 0001111111100011000 # xor d, opd\nxxx10000011001001111 0010011111100100000 # xor e, opd\nxxx10000011001011111 0010111111100101000 # xor bp, opd\nxxx10000011001101111 0011011111100110000 # xor sp, opd\nxxx10000011100001111 0000011111110000000 # shr a, opd\nxxx10000011100011111 0000111111110001000 # shr b, opd\nxxx10000011100101111 0001011111110010000 # shr c, opd\nxxx10000011100111111 0001111111110011000 # shr d, opd\nxxx10000011101001111 0010011111110100000 # shr e, opd\nxxx10000011101011111 0010111111110101000 # shr bp, opd\nxxx10000011101101111 0011011111110110000 # shr sp, opd\nxxx10000000000001001 0100110000000000010 # add a, [memaddr+opd]\nxxx10000000000011001 0100110010000001010 # add b, [memaddr+opd]\nxxx10000000000101001 0100110100000010010 # add c, [memaddr+opd]\nxxx10000000000111001 0100110110000011010 # add d, [memaddr+opd]\nxxx10000000001001001 0100111000000100010 # add e, [memaddr+opd]\nxxx10000000001011001 0100111010000101010 # add bp, [memaddr+opd]\nxxx10000000001101001 0100111100000110010 # add sp, [memaddr+opd]\nxxx10000000100001001 0100110000010000010 # sub a, [memaddr+opd]\nxxx10000000100011001 0100110010010001010 # sub b, [memaddr+opd]\nxxx10000000100101001 0100110100010010010 # sub c, [memaddr+opd]\nxxx10000000100111001 0100110110010011010 # sub d, [memaddr+opd]\nxxx10000000101001001 0100111000010100010 # sub e, [memaddr+opd]\nxxx10000000101011001 0100111010010101010 # sub bp, [memaddr+opd]\nxxx10000000101101001 0100111100010110010 # sub sp, [memaddr+opd]\nxxx10000001000001001 0100110000100000010 # mul a, [memaddr+opd]\nxxx10000001000011001 0100110010100001010 # mul b, [memaddr+opd]\nxxx10000001000101001 0100110100100010010 # mul c, [memaddr+opd]\nxxx10000001000111001 0100110110100011010 # mul d, [memaddr+opd]\nxxx10000001001001001 0100111000100100010 # mul e, [memaddr+opd]\nxxx10000001001011001 0100111010100101010 # mul bp, [memaddr+opd]\nxxx10000001001101001 0100111100100110010 # mul sp, [memaddr+opd]\nxxx10000001100001001 0100110000110000010 # and a, [memaddr+opd]\nxxx10000001100011001 0100110010110001010 # and b, [memaddr+opd]\nxxx10000001100101001 0100110100110010010 # and c, [memaddr+opd]\nxxx10000001100111001 0100110110110011010 # and d, [memaddr+opd]\nxxx10000001101001001 0100111000110100010 # and e, [memaddr+opd]\nxxx10000001101011001 0100111010110101010 # and bp, [memaddr+opd]\nxxx10000001101101001 0100111100110110010 # and sp, [memaddr+opd]\nxxx10000010000001001 0100110001000000010 # or a, [memaddr+opd]\nxxx10000010000011001 0100110011000001010 # or b, [memaddr+opd]\nxxx10000010000101001 0100110101000010010 # or c, [memaddr+opd]\nxxx10000010000111001 0100110111000011010 # or d, [memaddr+opd]\nxxx10000010001001001 0100111001000100010 # or e, [memaddr+opd]\nxxx10000010001011001 0100111011000101010 # or bp, [memaddr+opd]\nxxx10000010001101001 0100111101000110010 # or sp, [memaddr+opd]\nxxx10000011000001001 0100110001100000010 # xor a, [memaddr+opd]\nxxx10000011000011001 0100110011100001010 # xor b, [memaddr+opd]\nxxx10000011000101001 0100110101100010010 # xor c, [memaddr+opd]\nxxx10000011000111001 0100110111100011010 # xor d, [memaddr+opd]\nxxx10000011001001001 0100111001100100010 # xor e, [memaddr+opd]\nxxx10000011001011001 0100111011100101010 # xor bp, [memaddr+opd]\nxxx10000011001101001 0100111101100110010 # xor sp, [memaddr+opd]\nxxx10000011100001001 0100110001110000010 # shr a, [memaddr+opd]\nxxx10000011100011001 0100110011110001010 # shr b, [memaddr+opd]\nxxx10000011100101001 0100110101110010010 # shr c, [memaddr+opd]\nxxx10000011100111001 0100110111110011010 # shr d, [memaddr+opd]\nxxx10000011101001001 0100111001110100010 # shr e, [memaddr+opd]\nxxx10000011101011001 0100111011110101010 # shr bp, [memaddr+opd]\nxxx10000011101101001 0100111101110110010 # shr sp, [memaddr+opd]\nxxx10000000010111111 0101111110001010000 # add memval,opd\nxxx10000010100001111 0000010001010000000 # not a\nxxx10000010100011111 0000110001010001000 # not b\nxxx10000010100101111 0001010001010010000 # not c\nxxx10000010100111111 0001110001010011000 # not d\nxxx10000010101001111 0010010001010100000 # not e\nxxx10000010101011111 0010110001010101000 # not bp\nxxx10000010101101111 0011010001010110000 # not sp\nxxx10000100000000000 0000000000000000000 # mov a, a\nxxx10000100000000001 0000100000000000000 # mov a, b\nxxx10000100000000010 0001000000000000000 # mov a, c\nxxx10000100000000011 0001100000000000000 # mov a, d\nxxx10000100000000100 0010000000000000000 # mov a, e\nxxx10000100000000101 0010100000000000000 # mov a, bp\nxxx10000100000000110 0011000000000000000 # mov a, sp\nxxx10000100000010000 0000000000000001000 # mov b, a\nxxx10000100000010001 0000100000000001000 # mov b, b\nxxx10000100000010010 0001000000000001000 # mov b, c\nxxx10000100000010011 0001100000000001000 # mov b, d\nxxx10000100000010100 0010000000000001000 # mov b, e\nxxx10000100000010101 0010100000000001000 # mov b, bp\nxxx10000100000010110 0011000000000001000 # mov b, sp\nxxx10000100000100000 0000000000000010000 # mov c, a\nxxx10000100000100001 0000100000000010000 # mov c, b\nxxx10000100000100010 0001000000000010000 # mov c, c\nxxx10000100000100011 0001100000000010000 # mov c, d\nxxx10000100000100100 0010000000000010000 # mov c, e\nxxx10000100000100101 0010100000000010000 # mov c, bp\nxxx10000100000100110 0011000000000010000 # mov c, sp\nxxx10000100000110000 0000000000000011000 # mov d, a\nxxx10000100000110001 0000100000000011000 # mov d, b\nxxx10000100000110010 0001000000000011000 # mov d, c\nxxx10000100000110011 0001100000000011000 # mov d, d\nxxx10000100000110100 0010000000000011000 # mov d, e\nxxx10000100000110101 0010100000000011000 # mov d, bp\nxxx10000100000110110 0011000000000011000 # mov d, sp\nxxx10000100001000000 0000000000000100000 # mov e, a\nxxx10000100001000001 0000100000000100000 # mov e, b\nxxx10000100001000010 0001000000000100000 # mov e, c\nxxx10000100001000011 0001100000000100000 # mov e, d\nxxx10000100001000100 0010000000000100000 # mov e, e\nxxx10000100001000101 0010100000000100000 # mov e, bp\nxxx10000100001000110 0011000000000100000 # mov e, sp\nxxx10000100001010000 0000000000000101000 # mov bp, a\nxxx10000100001010001 0000100000000101000 # mov bp, b\nxxx10000100001010010 0001000000000101000 # mov bp, c\nxxx10000100001010011 0001100000000101000 # mov bp, d\nxxx10000100001010100 0010000000000101000 # mov bp, e\nxxx10000100001010101 0010100000000101000 # mov bp, bp\nxxx10000100001010110 0011000000000101000 # mov bp, sp\nxxx10000100001100000 0000000000000110000 # mov sp, a\nxxx10000100001100001 0000100000000110000 # mov sp, b\nxxx10000100001100010 0001000000000110000 # mov sp, c\nxxx10000100001100011 0001100000000110000 # mov sp, d\nxxx10000100001100100 0010000000000110000 # mov sp, e\nxxx10000100001100101 0010100000000110000 # mov sp, bp\nxxx10000100001100110 0011000000000110000 # mov sp, sp\nxxx10000100000001001 0100100000000000010 # mov a, [memaddr+opd]\nxxx10000100000011001 0100100000000001010 # mov b, [memaddr+opd]\nxxx10000100000101001 0100100000000010010 # mov c, [memaddr+opd]\nxxx10000100000111001 0100100000000011010 # mov d, [memaddr+opd]\nxxx10000100001001001 0100100000000100010 # mov e, [memaddr+opd]\nxxx10000100001011001 0100100000000101010 # mov bp, [memaddr+opd]\nxxx10000100001101001 0100100000000110010 # mov sp, [memaddr+opd]\nxxx10000100010111001 0100100000001010010 # mov memval, [memaddr+opd]\nxxx10000100010100000 0000000000001001000 # mov memaddr,a\nxxx10000100010100001 0000100000001001000 # mov memaddr,b\nxxx10000100010100010 0001000000001001000 # mov memaddr,c\nxxx10000100010100011 0001100000001001000 # mov memaddr,d\nxxx10000100010100100 0010000000001001000 # mov memaddr,e\nxxx10000100010100101 0010100000001001000 # mov memaddr,bp\nxxx10000100010100110 0011000000001001000 # mov memaddr,sp\nxxx10000100010110000 0000000000001010000 # mov memval,a\nxxx10000100010110001 0000100000001010000 # mov memval,b\nxxx10000100010110010 0001000000001010000 # mov memval,c\nxxx10000100010110011 0001100000001010000 # mov memval,d\nxxx10000100010110100 0010000000001010000 # mov memval,e\nxxx10000100010110101 0010100000001010000 # mov memval,bp\nxxx10000100010110110 0011000000001010000 # mov memval,sp\nxxx10000100010101010 0000000000001111011 # mov [memaddr+opd],memval\nxxx10000100010101111 0011100000001001000 # mov memaddr, opd\nxxx10000100010111111 0011100000001010000 # mov memval, opd\nxxx10000100000001111 0011100000000000000 # mov a, opd\nxxx10000100000011111 0011100000000001000 # mov b, opd\nxxx10000100000101111 0011100000000010000 # mov c, opd\nxxx10000100000111111 0011100000000011000 # mov d, opd\nxxx10000100001001111 0011100000000100000 # mov e, opd\nxxx10000100001011111 0011100000000101000 # mov bp, opd\nxxx10000100001101111 0011100000000110000 # mov sp, opd\nxxx10000100100001111 0100000000000000000 # in a\nxxx10000100100011111 0100000000000001000 # in b\nxxx10000100100101111 0100000000000010000 # in c\nxxx10000100100111111 0100000000000011000 # in d\nxxx10000100101001111 0100000000000100000 # in e\nxxx10000100101011111 0100000000000101000 # in bp\nxxx10000100101101111 0100000000000110000 # in sp\nxxx10000101000001111 0000000000001000000 # out a\nxxx10000101000011111 0000100000001000000 # out b\nxxx10000101000101111 0001000000001000000 # out c\nxxx10000101000111111 0001100000001000000 # out d\nxxx10000101001001111 0010000000001000000 # out e\nxxx10000101001011111 0010100000001000000 # out bp\nxxx10000101001101111 0011000000001000000 # out sp\nxxx10000101011111111 0011100000001000000 # out opd\nxxx10001001000000000 0000010000011111000 # cmp a, a\nxxx10001001000000001 0000010010011111000 # cmp a, b\nxxx10001001000000010 0000010100011111000 # cmp a, c\nxxx10001001000000011 0000010110011111000 # cmp a, d\nxxx10001001000000100 0000011000011111000 # cmp a, e\nxxx10001001000000101 0000011010011111000 # cmp a, bp\nxxx10001001000000110 0000011100011111000 # cmp a, sp\nxxx10001001000010000 0000110000011111000 # cmp b, a\nxxx10001001000010001 0000110010011111000 # cmp b, b\nxxx10001001000010010 0000110100011111000 # cmp b, c\nxxx10001001000010011 0000110110011111000 # cmp b, d\nxxx10001001000010100 0000111000011111000 # cmp b, e\nxxx10001001000010101 0000111010011111000 # cmp b, bp\nxxx10001001000010110 0000111100011111000 # cmp b, sp\nxxx10001001000100000 0001010000011111000 # cmp c, a\nxxx10001001000100001 0001010010011111000 # cmp c, b\nxxx10001001000100010 0001010100011111000 # cmp c, c\nxxx10001001000100011 0001010110011111000 # cmp c, d\nxxx10001001000100100 0001011000011111000 # cmp c, e\nxxx10001001000100101 0001011010011111000 # cmp c, bp\nxxx10001001000100110 0001011100011111000 # cmp c, sp\nxxx10001001000110000 0001110000011111000 # cmp d, a\nxxx10001001000110001 0001110010011111000 # cmp d, b\nxxx10001001000110010 0001110100011111000 # cmp d, c\nxxx10001001000110011 0001110110011111000 # cmp d, d\nxxx10001001000110100 0001111000011111000 # cmp d, e\nxxx10001001000110101 0001111010011111000 # cmp d, bp\nxxx10001001000110110 0001111100011111000 # cmp d, sp\nxxx10001001001000000 0010010000011111000 # cmp e, a\nxxx10001001001000001 0010010010011111000 # cmp e, b\nxxx10001001001000010 0010010100011111000 # cmp e, c\nxxx10001001001000011 0010010110011111000 # cmp e, d\nxxx10001001001000100 0010011000011111000 # cmp e, e\nxxx10001001001000101 0010011010011111000 # cmp e, bp\nxxx10001001001000110 0010011100011111000 # cmp e, sp\nxxx10001001001010000 0010110000011111000 # cmp bp, a\nxxx10001001001010001 0010110010011111000 # cmp bp, b\nxxx10001001001010010 0010110100011111000 # cmp bp, c\nxxx10001001001010011 0010110110011111000 # cmp bp, d\nxxx10001001001010100 0010111000011111000 # cmp bp, e\nxxx10001001001010101 0010111010011111000 # cmp bp, bp\nxxx10001001001010110 0010111100011111000 # cmp bp, sp\nxxx10001001001100000 0011010000011111000 # cmp sp, a\nxxx10001001001100001 0011010010011111000 # cmp sp, b\nxxx10001001001100010 0011010100011111000 # cmp sp, c\nxxx10001001001100011 0011010110011111000 # cmp sp, d\nxxx10001001001100100 0011011000011111000 # cmp sp, e\nxxx10001001001100101 0011011010011111000 # cmp sp, bp\nxxx10001001001100110 0011011100011111000 # cmp sp, sp\nxxx10001001000001111 0000011110011111000 # cmp a, opd\nxxx10001001000011111 0000111110011111000 # cmp b, opd\nxxx10001001000101111 0001011110011111000 # cmp c, opd\nxxx10001001000111111 0001111110011111000 # cmp d, opd\nxxx10001001001001111 0010011110011111000 # cmp e, opd\nxxx10001001001011111 0010111110011111000 # cmp bp, opd\nxxx10001001001101111 0011011110011111000 # cmp sp, opd\nxxx10001000110111111 0101100000000111000 # jmp memval\n0xx10000101100001111 0000000000000111000 # jnc a (Taken)\n0xx10000101100011111 0000100000000111000 # jnc b (Taken)\n0xx10000101100101111 0001000000000111000 # jnc c (Taken)\n0xx10000101100111111 0001100000000111000 # jnc d (Taken)\n0xx10000101101001111 0010000000000111000 # jnc e (Taken)\n0xx10000101101011111 0010100000000111000 # jnc bp (Taken)\n0xx10000101101101111 0011000000000111000 # jnc sp (Taken)\n1xx10000101100001111 0000000000001111000 # jnc a (Skip)\n1xx10000101100011111 0000000000001111000 # jnc b (Skip)\n1xx10000101100101111 0000000000001111000 # jnc c (Skip)\n1xx10000101100111111 0000000000001111000 # jnc d (Skip)\n1xx10000101101001111 0000000000001111000 # jnc e (Skip)\n1xx10000101101011111 0000000000001111000 # jnc bp (Skip)\n1xx10000101101101111 0000000000001111000 # jnc sp (Skip)\n1xx10000110000001111 0000000000000111000 # jc a (Taken)\n1xx10000110000011111 0000100000000111000 # jc b (Taken)\n1xx10000110000101111 0001000000000111000 # jc c (Taken)\n1xx10000110000111111 0001100000000111000 # jc d (Taken)\n1xx10000110001001111 0010000000000111000 # jc e (Taken)\n1xx10000110001011111 0010100000000111000 # jc bp (Taken)\n1xx10000110001101111 0011000000000111000 # jc sp (Taken)\n0xx10000110000001111 0000000000001111000 # jc a (Skip)\n0xx10000110000011111 0000000000001111000 # jc b (Skip)\n0xx10000110000101111 0000000000001111000 # jc c (Skip)\n0xx10000110000111111 0000000000001111000 # jc d (Skip)\n0xx10000110001001111 0000000000001111000 # jc e (Skip)\n0xx10000110001011111 0000000000001111000 # jc bp (Skip)\n0xx10000110001101111 0000000000001111000 # jc sp (Skip)\nx0x10000110100001111 0000000000000111000 # jnz a (Taken)\nx0x10000110100011111 0000100000000111000 # jnz b (Taken)\nx0x10000110100101111 0001000000000111000 # jnz c (Taken)\nx0x10000110100111111 0001100000000111000 # jnz d (Taken)\nx0x10000110101001111 0010000000000111000 # jnz e (Taken)\nx0x10000110101011111 0010100000000111000 # jnz bp (Taken)\nx0x10000110101101111 0011000000000111000 # jnz sp (Taken)\nx1x10000110100001111 0000000000001111000 # jnz a (Skip)\nx1x10000110100011111 0000000000001111000 # jnz b (Skip)\nx1x10000110100101111 0000000000001111000 # jnz c (Skip)\nx1x10000110100111111 0000000000001111000 # jnz d (Skip)\nx1x10000110101001111 0000000000001111000 # jnz e (Skip)\nx1x10000110101011111 0000000000001111000 # jnz bp (Skip)\nx1x10000110101101111 0000000000001111000 # jnz sp (Skip)\nx1x10000111000001111 0000000000000111000 # jz a (Taken)\nx1x10000111000011111 0000100000000111000 # jz b (Taken)\nx1x10000111000101111 0001000000000111000 # jz c (Taken)\nx1x10000111000111111 0001100000000111000 # jz d (Taken)\nx1x10000111001001111 0010000000000111000 # jz e (Taken)\nx1x10000111001011111 0010100000000111000 # jz bp (Taken)\nx1x10000111001101111 0011000000000111000 # jz sp (Taken)\nx0x10000111000001111 0000000000001111000 # jz a (Skip)\nx0x10000111000011111 0000000000001111000 # jz b (Skip)\nx0x10000111000101111 0000000000001111000 # jz c (Skip)\nx0x10000111000111111 0000000000001111000 # jz d (Skip)\nx0x10000111001001111 0000000000001111000 # jz e (Skip)\nx0x10000111001011111 0000000000001111000 # jz bp (Skip)\nx0x10000111001101111 0000000000001111000 # jz sp (Skip)\nxx010000111100001111 0000000000000111000 # jns a (Taken)\nxx010000111100011111 0000100000000111000 # jns b (Taken)\nxx010000111100101111 0001000000000111000 # jns c (Taken)\nxx010000111100111111 0001100000000111000 # jns d (Taken)\nxx010000111101001111 0010000000000111000 # jns e (Taken)\nxx010000111101011111 0010100000000111000 # jns bp (Taken)\nxx010000111101101111 0011000000000111000 # jns sp (Taken)\nxx110000111100001111 0000000000001111000 # jns a (Skip)\nxx110000111100011111 0000000000001111000 # jns b (Skip)\nxx110000111100101111 0000000000001111000 # jns c (Skip)\nxx110000111100111111 0000000000001111000 # jns d (Skip)\nxx110000111101001111 0000000000001111000 # jns e (Skip)\nxx110000111101011111 0000000000001111000 # jns bp (Skip)\nxx110000111101101111 0000000000001111000 # jns sp (Skip)\nxx110001000000001111 0000000000000111000 # js a (Taken)\nxx110001000000011111 0000100000000111000 # js b (Taken)\nxx110001000000101111 0001000000000111000 # js c (Taken)\nxx110001000000111111 0001100000000111000 # js d (Taken)\nxx110001000001001111 0010000000000111000 # js e (Taken)\nxx110001000001011111 0010100000000111000 # js bp (Taken)\nxx110001000001101111 0011000000000111000 # js sp (Taken)\nxx010001000000001111 0000000000001111000 # js a (Skip)\nxx010001000000011111 0000000000001111000 # js b (Skip)\nxx010001000000101111 0000000000001111000 # js c (Skip)\nxx010001000000111111 0000000000001111000 # js d (Skip)\nxx010001000001001111 0000000000001111000 # js e (Skip)\nxx010001000001011111 0000000000001111000 # js bp (Skip)\nxx010001000001101111 0000000000001111000 # js sp (Skip)\nxxx10001000100001111 0000000000000111000 # jmp a\nxxx10001000100011111 0000100000000111000 # jmp b\nxxx10001000100101111 0001000000000111000 # jmp c\nxxx10001000100111111 0001100000000111000 # jmp d\nxxx10001000101001111 0010000000000111000 # jmp e\nxxx10001000101011111 0010100000000111000 # jmp bp\nxxx10001000101101111 0011000000000111000 # jmp sp\nx1x10001011000001111 0000000000000111000 # je a (Taken)\nx1x10001011000011111 0000100000000111000 # je b (Taken)\nx1x10001011000101111 0001000000000111000 # je c (Taken)\nx1x10001011000111111 0001100000000111000 # je d (Taken)\nx1x10001011001001111 0010000000000111000 # je e (Taken)\nx1x10001011001011111 0010100000000111000 # je bp (Taken)\nx1x10001011001101111 0011000000000111000 # je sp (Taken)\nx0x10001011000001111 0000000000001111000 # je a (Skip)\nx0x10001011000011111 0000000000001111000 # je b (Skip)\nx0x10001011000101111 0000000000001111000 # je c (Skip)\nx0x10001011000111111 0000000000001111000 # je d (Skip)\nx0x10001011001001111 0000000000001111000 # je e (Skip)\nx0x10001011001011111 0000000000001111000 # je bp (Skip)\nx0x10001011001101111 0000000000001111000 # je sp (Skip)\nx0x10001011100001111 0000000000000111000 # jne a(Taken)\nx0x10001011100011111 0000100000000111000 # jne b(Taken)\nx0x10001011100101111 0001000000000111000 # jne c(Taken)\nx0x10001011100111111 0001100000000111000 # jne d(Taken)\nx0x10001011101001111 0010000000000111000 # jne e(Taken)\nx0x10001011101011111 0010100000000111000 # jne bp(Taken)\nx0x10001011101101111 0011000000000111000 # jne sp(Taken)\nx1x10001011100001111 0000000000001111000 # jne a(Skip)\nx1x10001011100011111 0000000000001111000 # jne b(Skip)\nx1x10001011100101111 0000000000001111000 # jne c(Skip)\nx1x10001011100111111 0000000000001111000 # jne d(Skip)\nx1x10001011101001111 0000000000001111000 # jne e(Skip)\nx1x10001011101011111 0000000000001111000 # jne bp(Skip)\nx1x10001011101101111 0000000000001111000 # jne sp(Skip)\nx0010001100000001111 0000000000000111000 # ja a (Taken)\nx0010001100000011111 0000100000000111000 # ja b (Taken)\nx0010001100000101111 0001000000000111000 # ja c (Taken)\nx0010001100000111111 0001100000000111000 # ja d (Taken)\nx0010001100001001111 0010000000000111000 # ja e (Taken)\nx0010001100001011111 0010100000000111000 # ja bp (Taken)\nx0010001100001101111 0011000000000111000 # ja sp (Taken)\nxxx10001100000001111 0000000000001111000 # ja a (Skip)\nxxx10001100000011111 0000000000001111000 # ja b (Skip)\nxxx10001100000101111 0000000000001111000 # ja c (Skip)\nxxx10001100000111111 0000000000001111000 # ja d (Skip)\nxxx10001100001001111 0000000000001111000 # ja e (Skip)\nxxx10001100001011111 0000000000001111000 # ja bp (Skip)\nxxx10001100001101111 0000000000001111000 # ja sp (Skip)\nx0010001100100001111 0000000000000111000 # jae a (Taken)\nx0010001100100011111 0000100000000111000 # jae b (Taken)\nx0010001100100101111 0001000000000111000 # jae c (Taken)\nx0010001100100111111 0001100000000111000 # jae d (Taken)\nx0010001100101001111 0010000000000111000 # jae e (Taken)\nx0010001100101011111 0010100000000111000 # jae bp (Taken)\nx0010001100101101111 0011000000000111000 # jae sp (Taken)\nx1010001100100001111 0000000000000111000 # jae a (Taken)\nx1010001100100011111 0000100000000111000 # jae b (Taken)\nx1010001100100101111 0001000000000111000 # jae c (Taken)\nx1010001100100111111 0001100000000111000 # jae d (Taken)\nx1010001100101001111 0010000000000111000 # jae e (Taken)\nx1010001100101011111 0010100000000111000 # jae bp (Taken)\nx1010001100101101111 0011000000000111000 # jae sp (Taken)\nxxx10001100100001111 0000000000001111000 # jae a (Skip)\nxxx10001100100011111 0000000000001111000 # jae b (Skip)\nxxx10001100100101111 0000000000001111000 # jae c (Skip)\nxxx10001100100111111 0000000000001111000 # jae d (Skip)\nxxx10001100101001111 0000000000001111000 # jae e (Skip)\nxxx10001100101011111 0000000000001111000 # jae bp (Skip)\nxxx10001100101101111 0000000000001111000 # jae sp (Skip)\nx0110001101000001111 0000000000000111000 # jl a (Taken)\nx0110001101000011111 0000100000000111000 # jl b (Taken)\nx0110001101000101111 0001000000000111000 # jl c (Taken)\nx0110001101000111111 0001100000000111000 # jl d (Taken)\nx0110001101001001111 0010000000000111000 # jl e (Taken)\nx0110001101001011111 0010100000000111000 # jl bp (Taken)\nx0110001101001101111 0011000000000111000 # jl sp (Taken)\nxxx10001101000001111 0000000000001111000 # jl a (Skip)\nxxx10001101000011111 0000000000001111000 # jl b (Skip)\nxxx10001101000101111 0000000000001111000 # jl c (Skip)\nxxx10001101000111111 0000000000001111000 # jl d (Skip)\nxxx10001101001001111 0000000000001111000 # jl e (Skip)\nxxx10001101001011111 0000000000001111000 # jl bp (Skip)\nxxx10001101001101111 0000000000001111000 # jl sp (Skip)\nx0110001101100001111 0000000000000111000 # jle a (Taken)\nx0110001101100011111 0000100000000111000 # jle b (Taken)\nx0110001101100101111 0001000000000111000 # jle c (Taken)\nx0110001101100111111 0001100000000111000 # jle d (Taken)\nx0110001101101001111 0010000000000111000 # jle e (Taken)\nx0110001101101011111 0010100000000111000 # jle bp (Taken)\nx0110001101101101111 0011000000000111000 # jle sp (Taken)\nx1010001101100001111 0000000000000111000 # jle a (Taken)\nx1010001101100011111 0000100000000111000 # jle b (Taken)\nx1010001101100101111 0001000000000111000 # jle c (Taken)\nx1010001101100111111 0001100000000111000 # jle d (Taken)\nx1010001101101001111 0010000000000111000 # jle e (Taken)\nx1010001101101011111 0010100000000111000 # jle bp (Taken)\nx1010001101101101111 0011000000000111000 # jle sp (Taken)\nxxx10001101100001111 0000000000001111000 # jle a (Skip)\nxxx10001101100011111 0000000000001111000 # jle b (Skip)\nxxx10001101100101111 0000000000001111000 # jle c (Skip)\nxxx10001101100111111 0000000000001111000 # jle d (Skip)\nxxx10001101101001111 0000000000001111000 # jle e (Skip)\nxxx10001101101011111 0000000000001111000 # jle bp (Skip)\nxxx10001101101101111 0000000000001111000 # jle sp (Skip)")) Instruction_Decoder (
    .in({carry_flag, zero_flag, sign_flag, IE, Instruction_Register_p5}),
    .out({CPU_Control_BUS, Instruction_Decoder_out[0]}));
endmodule

module registers (
  input  [15:0] reg_data_in,
  input  CLK,
  input  RESET,
  input  [15:0] write_reg_select,
  output [15:0] memval_out,
  output [15:0] memaddr_out,
  output [15:0] a_out,
  output [15:0] b_out,
  output [15:0] c_out,
  output [15:0] d_out,
  output [15:0] e_out,
  output [15:0] bp_out,
  output [15:0] sp_out,
  output [15:0] output_out
);

  Register #(.width(16)) MEMVAL (.D(reg_data_in), .en(write_reg_select[10]), .clk(CLK), .Q(memval_out), .clr(RESET));
  Register #(.width(16)) MEMADDR (.D(reg_data_in), .en(write_reg_select[9]), .clk(CLK), .Q(memaddr_out), .clr(RESET));
  Register #(.width(16)) A (.D(reg_data_in), .en(write_reg_select[0]), .clk(CLK), .Q(a_out), .clr(RESET));
  Register #(.width(16)) B (.D(reg_data_in), .en(write_reg_select[1]), .clk(CLK), .Q(b_out), .clr(RESET));
  Register #(.width(16)) C (.D(reg_data_in), .en(write_reg_select[2]), .clk(CLK), .Q(c_out), .clr(RESET));
  Register #(.width(16)) D (.D(reg_data_in), .en(write_reg_select[3]), .clk(CLK), .Q(d_out), .clr(RESET));
  Register #(.width(16)) E (.D(reg_data_in), .en(write_reg_select[4]), .clk(CLK), .Q(e_out), .clr(RESET));
  Register #(.width(16)) BP (.D(reg_data_in), .en(write_reg_select[5]), .clk(CLK), .Q(bp_out), .clr(RESET));
  Register #(.width(16)) SP (.D(reg_data_in), .en(write_reg_select[6]), .clk(CLK), .Q(sp_out), .clr(RESET));
  Register #(.width(16)) Output_port (
    .D(reg_data_in), .en(write_reg_select[8]), .clk(CLK), .Q(output_out), .clr(RESET));
endmodule

module ALU (
  input  [15:0] in1_data_in,
  input  [15:0] in2_data_in,
  input  [2:0] ALU_function_select,
  output [15:0] ALU_Out,
  output sign_flag,
  output zero_flag,
  output carry_flag
);

  wire adder_1_cout, not_2_out, not_3_out, not_4_out, not_5_out, not_6_out, not_7_out, not_8_out, not_9_out,
       not_10_out, not_11_out, not_12_out, not_13_out, not_14_out, not_15_out, not_16_out, not_17_out,
       right_shifter_1_carry_out;
  wire [15:0] adder_1_out, and_1_out, demultiplexer_1_out0, demultiplexer_1_out1, demultiplexer_1_out2,
       demultiplexer_1_out3, demultiplexer_1_out4, demultiplexer_1_out5, demultiplexer_1_out6,
       demultiplexer_1_out7, demultiplexer_2_out0, demultiplexer_2_out1, demultiplexer_2_out2,
       demultiplexer_2_out3, demultiplexer_2_out4, demultiplexer_2_out6, demultiplexer_2_out7,
       multiplier_1_cout, multiplier_1_out, not_1_out, or_1_out, right_shifter_1_output_bus_1,
       subtractor_1_out, xor_1_out;

  Demultiplexer #(.select(3), .width(16)) demultiplexer_1 (
    .out0(demultiplexer_1_out0), .out1(demultiplexer_1_out1), .out2(demultiplexer_1_out2),
    .out3(demultiplexer_1_out3), .out4(demultiplexer_1_out4), .out5(demultiplexer_1_out5),
    .out6(demultiplexer_1_out6), .out7(demultiplexer_1_out7), .in(in1_data_in), .sel(ALU_function_select));
  Demultiplexer #(.select(3), .width(16)) demultiplexer_2 (
    .out0(demultiplexer_2_out0), .out1(demultiplexer_2_out1), .out2(demultiplexer_2_out2),
    .out3(demultiplexer_2_out3), .out4(demultiplexer_2_out4), .out6(demultiplexer_2_out6),
    .out7(demultiplexer_2_out7), .in(in2_data_in), .sel(ALU_function_select));  // open: out5
  Adder #(.width(16)) adder_1 (
    .a(demultiplexer_1_out0), .b(demultiplexer_2_out0), .out(adder_1_out), .cin(1'b0), .cout(adder_1_cout));
  Subtractor #(.width(16)) subtractor_1 (
    .a(demultiplexer_1_out1), .b(demultiplexer_2_out1), .out(subtractor_1_out), .bin(1'b0), .bout(sign_flag));
  Multiplier #(.width(16)) multiplier_1 (
    .a(demultiplexer_1_out2), .b(demultiplexer_2_out2), .out(multiplier_1_out), .cin({16{1'b0}}),
    .cout(multiplier_1_cout));
  assign and_1_out = demultiplexer_1_out3 & demultiplexer_2_out3;  // AND_Gate and_1, 16 bits wide
  assign or_1_out = demultiplexer_1_out4 | demultiplexer_2_out4;  // OR_Gate or_1, 16 bits wide
  assign not_1_out = ~demultiplexer_1_out5;  // NOT_Gate not_1, 16 bits wide
  assign xor_1_out = demultiplexer_1_out6 ^ demultiplexer_2_out6;  // XOR_Gate xor_1, 16 bits wide
  right_shifter right_shifter_1 (
    .Input_bus_1(demultiplexer_2_out7), .Input_bus_2(demultiplexer_1_out7),
    .carry_out(right_shifter_1_carry_out), .Output_bus_1(right_shifter_1_output_bus_1));
  Multiplexer #(.select(3), .width(16)) multiplexer_1 (
    .in0(adder_1_out), .in1(subtractor_1_out), .in2(multiplier_1_out), .in3(and_1_out), .in4(or_1_out),
    .in5(not_1_out), .in6(xor_1_out), .in7(right_shifter_1_output_bus_1), .out(ALU_Out),
    .sel(ALU_function_select));
  or or_2 (carry_flag, adder_1_cout, multiplier_1_cout[7], multiplier_1_cout[0], multiplier_1_cout[1], multiplier_1_cout[2], multiplier_1_cout[3], multiplier_1_cout[4], multiplier_1_cout[5], multiplier_1_cout[6], multiplier_1_cout[8], multiplier_1_cout[9], multiplier_1_cout[10], multiplier_1_cout[11], multiplier_1_cout[12], multiplier_1_cout[13], multiplier_1_cout[14], multiplier_1_cout[15], right_shifter_1_carry_out);
  not not_2 (not_2_out, ALU_Out[0]);
  not not_3 (not_3_out, ALU_Out[1]);
  not not_4 (not_4_out, ALU_Out[2]);
  not not_5 (not_5_out, ALU_Out[3]);
  not not_6 (not_6_out, ALU_Out[4]);
  not not_7 (not_7_out, ALU_Out[5]);
  not not_8 (not_8_out, ALU_Out[6]);
  not not_9 (not_9_out, ALU_Out[7]);
  not not_10 (not_10_out, ALU_Out[8]);
  not not_11 (not_11_out, ALU_Out[9]);
  not not_12 (not_12_out, ALU_Out[10]);
  not not_13 (not_13_out, ALU_Out[11]);
  not not_14 (not_14_out, ALU_Out[12]);
  not not_15 (not_15_out, ALU_Out[13]);
  not not_16 (not_16_out, ALU_Out[14]);
  not not_17 (not_17_out, ALU_Out[15]);
  and and_2 (zero_flag, not_9_out, not_2_out, not_3_out, not_4_out, not_5_out, not_6_out, not_7_out, not_8_out, not_10_out, not_11_out, not_12_out, not_13_out, not_14_out, not_15_out, not_16_out, not_17_out);
endmodule
